// Logisim project Lab 1.circ as structural Verilog: 10 circuits, main circuit Main
module Main (
);

  wire Clock, Logging, ROMSequentialOutput, sequential_input_1_not_done, X;
  wire [2:0] CombinationalOutput, ROMCombinationalOutput;
  wire [7:0] Input;

  Combinational_Input combinational_input_1 (
    .In7(Input[7]), .In6(Input[6]), .In5(Input[5]), .In4(Input[4]), .In3(Input[3]), .In2(Input[2]),
    .In1(Input[1]), .In0(Input[0]), .Clock(Clock));
  Sequential_Input sequential_input_1 (.X(X), .Logging(Logging), .Clock(Clock), .Not_Done(sequential_input_1_not_done));
  Clock clock_1 (.out(Clock));
  ROMsequen romsequen_1 (.YourX(X), .Sel(sequential_input_1_not_done), .Clock(Clock), .Out(ROMSequentialOutput));
  Combinational combinational_1 (
    .In7(Input[7]), .In6(Input[6]), .In5(Input[5]), .In4(Input[4]), .In3(Input[3]), .In2(Input[2]),
    .In1(Input[1]), .In0(Input[0]), .Out(CombinationalOutput));  // open: Out2, Out1, Out0
  ROM rom_1 (.In(Input), .Out(ROMCombinationalOutput));
  // Probe on Input
  // Probe on CombinationalOutput
  // Probe on ROMCombinationalOutput
  // Probe on Logging
  // Probe on X
  // Probe on ROMSequentialOutput
endmodule

module Combinational_Input (
  input  Clock,
  output In7,
  output In6,
  output In5,
  output In4,
  output In3,
  output In2,
  output In1,
  output In0
);

  wire [7:0] counter_1_q;

  Counter #(.ongoal("stay")) counter_1 (.count(1'b1), .Q(counter_1_q), .clk(Clock));  // open: load, D, carry, clr
  ROM_part rom_1 (.addr(counter_1_q), .data({In7, In6, In5, In4, In3, In2, In1, In0}));  // open: sel

  // Notes on the sheet:
  //   contents of rom_1 (hex, n*v repeats v):
  //   0 1 2 3 4 5 6 7 8 9 a b c d e f 10 11 12 13 14 15 16 17 18 19 1a 1b 1c 1d 1e 1f 20 21 22 23 24 25 26
  //   27 28 29 2a 2b 2c 2d 2e 2f 30 31 32 33 34 35 36 37 38 39 3a 3b 3c 3d 3e 3f 40 41 42 43 44 45 46 47
  //   48 49 4a 4b 4c 4d 4e 4f 50 51 52 53 54 55 56 57 58 59 5a 5b 5c 5d 5e 5f 60 61 62 63 64 65 66 67 68
  //   69 6a 6b 6c 6d 6e 6f 70 71 72 73 74 75 76 77 78 79 7a 7b 7c 7d 7e 7f 80 81 82 83 84 85 86 87 88 89
  //   8a 8b 8c 8d 8e 8f 90 91 92 93 94 95 96 97 98 99 9a 9b 9c 9d 9e 9f a0 a1 a2 a3 a4 a5 a6 a7 a8 a9 aa
  //   ab ac ad ae af b0 b1 b2 b3 b4 b5 b6 b7 b8 b9 ba bb bc bd be bf c0 c1 c2 c3 c4 c5 c6 c7 c8 c9 ca cb
  //   cc cd ce cf d0 d1 d2 d3 d4 d5 d6 d7 d8 d9 da db dc dd de df e0 e1 e2 e3 e4 e5 e6 e7 e8 e9 ea eb ec
  //   ed ee ef f0 f1 f2 f3 f4 f5 f6 f7 f8 f9 fa fb fc fd fe ff
endmodule

module Sequential_Input (
  input  Clock,
  output X,
  output Not_Done,
  output Logging
);

  wire counter_1_carry, not_2_out;
  wire [7:0] counter_1_q;

  Counter #(.max('h7f), .ongoal("stay")) counter_1 (
    .count(1'b1), .Q(counter_1_q), .carry(counter_1_carry), .clk(Clock));  // open: load, D, clr
  not not_1 (Not_Done, counter_1_carry);
  not not_2 (not_2_out, Logging);
  Register #(.width(1)) register_1 (.D(not_2_out), .en(Not_Done), .Q(Logging), .clk(Clock));  // open: clr
  ROM_part #(.dataWidth(1)) rom_1 (.addr(counter_1_q), .data(X));  // open: sel

  // Notes on the sheet:
  //   contents of rom_1 (hex, n*v repeats v):
  //   7*0 1 0 0 1 0 0 0 1 1 0 1 0 0 0 1 0 1 0 1 1 0 0 4*1 0 0 0 1 0 0 1 1 0 1 0 1 0 4*1 0 0 1 1 0 4*1 0
  //   4*1 0 1 1 1 6*0 5*1 0 0 1 0 1 1 0 0 0 1 0 6*1 0 1 7*0 1 1 1 0 1 4*0 5*1 0 0 1 4*0 1 1
endmodule

module ROM_XOR (
  input  X,
  input  Y,
  output X_XOR_Y
);

  ROM_part #(.addrWidth(2), .dataWidth(1)) rom_1 (.addr({X, Y}), .data(X_XOR_Y));  // open: sel

  // Notes on the sheet:
  //   contents of rom_1 (hex, n*v repeats v):
  //   0 1 1
endmodule

module ROM_Sequential (
  input  X,
  input  Clock,
  output [1:0] Out
);

  wire [1:1] register_1_q;
  wire [2:0] rom_1_data;

  ROM_part #(.addrWidth(2), .dataWidth(3)) rom_1 (.addr({register_1_q[1], X}), .data(rom_1_data));  // open: sel
  Register #(.width(3)) register_1 (.D(rom_1_data), .Q({register_1_q[1], Out}), .clk(Clock));  // open: en, clr

  // Notes on the sheet:
  //   contents of rom_1 (hex, n*v repeats v):
  //   1 5 7 3
endmodule

module ROM (
  input  [7:0] In,
  output [2:0] Out
);

  ROM_part #(.dataWidth(3)) rom_1 (.addr(In), .data(Out));  // open: sel

  // Notes on the sheet:
  //   contents of rom_1 (hex, n*v repeats v):
  //   0 7 1 4 6 3 2 4 0 0 5 53*0 16*1 112*0 16*2 16*3
endmodule

module ROMSeq (
  input  X,
  input  Not_Done,
  input  Clock,
  output Out
);

  wire [6:0] register_1_q;
  wire [7:0] rom_1_data;

  ROM_part rom_1 (.addr({register_1_q, X}), .data(rom_1_data), .sel(Not_Done));
  Register register_1 (.D(rom_1_data), .Q({register_1_q, Out}), .clk(Clock));  // open: en, clr

  // Notes on the sheet:
  //   contents of rom_1 (hex, n*v repeats v):
  //   2 4 6 8 a c e 10 12 14 16 18 1a 1c 1e 20 22 24 26 28 2a 2c 2e 30 32 34 36 38 3a 3c 3e 40 42 44 46 48
  //   4a 4c 4e 50 52 54 56 58 5a 3c 5e 60 62 64 66 68 6a 6c 6e 70 72 74 76 78 7a 7c 7e 80 82 84 86 88 8a
  //   8c 8e 90 92 94 96 98 9a 9c 9e a0 a2 a4 a6 a8 aa ac ae b0 b2 b4 b6 b8 ba bc be c0 c2 c4 c6 c8 ca cc
  //   ce d0 d2 d4 d6 d8 da dc de e0 e2 e4 e6 e8 ea ec ee f0 f2 f4 f6 f8 fa fc 30*0 1 1 14*0 1 1 6*0 1 1 0
  //   0 6*1 14*0 1 1 6*0 1 1 0 0 6*1 6*0 10*1 0 0 14*1
endmodule

// Comb
module Combin (
  input  In7,
  input  In6,
  input  In5,
  input  In4,
  input  In3,
  input  In2,
  input  In1,
  input  In0,
  output Out2,
  output [2:0] Out,
  output Out1,
  output Out0
);

  wire and_1_out, and_2_out, and_3_out, and_4_out, and_5_out, and_6_out, and_7_out, and_8_out, and_9_out,
       and_10_out, not_1_out, not_2_out, not_3_out, not_4_out, not_5_out, not_6_out, not_7_out, not_8_out,
       not_9_out, not_10_out, not_11_out, not_12_out, not_13_out, not_14_out, not_15_out, not_16_out,
       not_17_out, not_18_out, not_19_out, not_20_out, not_21_out, not_22_out, not_23_out, not_24_out,
       not_25_out, not_26_out, not_27_out, not_28_out, not_29_out, not_30_out, not_31_out, not_32_out,
       not_33_out, not_34_out, not_35_out, not_36_out, not_37_out, not_38_out, not_39_out, not_40_out,
       not_41_out, not_42_out, not_43_out, not_44_out;

  not not_1 (not_1_out, In7);
  not not_2 (not_2_out, In6);
  not not_3 (not_3_out, In5);
  not not_4 (not_4_out, In4);
  not not_5 (not_5_out, In3);
  not not_6 (not_6_out, In2);
  not not_7 (not_7_out, In7);
  not not_8 (not_8_out, In6);
  not not_9 (not_9_out, In5);
  not not_10 (not_10_out, In4);
  not not_11 (not_11_out, In3);
  not not_12 (not_12_out, In7);
  not not_13 (not_13_out, In6);
  not not_14 (not_14_out, In5);
  not not_15 (not_15_out, In4);
  not not_16 (not_16_out, In2);
  not not_17 (not_17_out, In0);
  not not_18 (not_18_out, In7);
  not not_19 (not_19_out, In6);
  not not_20 (not_20_out, In5);
  not not_21 (not_21_out, In4);
  not not_22 (not_22_out, In3);
  not not_23 (not_23_out, In1);
  not not_24 (not_24_out, In7);
  not not_25 (not_25_out, In6);
  not not_26 (not_26_out, In5);
  not not_27 (not_27_out, In4);
  not not_28 (not_28_out, In3);
  not not_29 (not_29_out, In0);
  not not_30 (not_30_out, In5);
  not not_31 (not_31_out, In7);
  not not_32 (not_32_out, In5);
  not not_33 (not_33_out, In4);
  not not_34 (not_34_out, In3);
  not not_35 (not_35_out, In1);
  not not_36 (not_36_out, In7);
  not not_37 (not_37_out, In5);
  not not_38 (not_38_out, In4);
  not not_39 (not_39_out, In2);
  not not_40 (not_40_out, In0);
  not not_41 (not_41_out, In7);
  not not_42 (not_42_out, In5);
  not not_43 (not_43_out, In4);
  not not_44 (not_44_out, In5);
  and and_1 (and_1_out, not_1_out, not_2_out, not_3_out, not_4_out, not_5_out, not_6_out, In0);
  and and_2 (and_2_out, not_7_out, not_8_out, not_9_out, not_10_out, not_11_out, In1, In0);
  and and_3 (and_3_out, not_12_out, not_13_out, not_14_out, not_15_out, In3, not_16_out, In1, not_17_out);
  and and_4 (and_4_out, not_18_out, not_19_out, not_20_out, not_21_out, not_22_out, not_23_out, In0);
  and and_5 (and_5_out, not_24_out, not_25_out, not_26_out, not_27_out, not_28_out, In2, not_29_out);
  and and_6 (and_6_out, In7, In6, not_30_out);
  and and_7 (and_7_out, not_31_out, not_32_out, not_33_out, not_34_out, not_35_out, In0);
  and and_8 (and_8_out, not_36_out, not_37_out, not_38_out, not_39_out, In1, not_40_out);
  and and_9 (and_9_out, not_41_out, In6, not_42_out, not_43_out);
  and and_10 (and_10_out, In7, In6, not_44_out, In4);
  or or_1 (Out[2], and_1_out, and_2_out, and_3_out);
  or or_2 (Out[1], and_4_out, and_5_out, and_6_out);
  or or_3 (Out[0], and_7_out, and_8_out, and_9_out, and_10_out);

  assign Out0 = Out[0];
  assign Out1 = Out[1];
  assign Out2 = Out[2];
endmodule

module ROMsequen (
  input  YourX,
  input  Sel,
  input  Clock,
  output Out
);

  wire [6:0] register_1_q;
  wire [7:0] rom_1_data;

  ROM_part rom_1 (.addr({register_1_q, YourX}), .data(rom_1_data), .sel(Sel));
  Register register_1 (.D(rom_1_data), .Q({register_1_q, Out}), .clk(Clock));  // open: en, clr

  // Notes on the sheet:
  //   contents of rom_1 (hex, n*v repeats v):
  //   2 4 6 8 a c e 10 12 14 16 18 1a 1c 1e 20 22 24 26 28 2a 2c 2e 30 32 34 36 38 3a 3c 3e 40 42 44 46 48
  //   4a 4c 4e 50 52 54 56 58 5a 3c 5e 60 62 64 66 68 6a 6c 6e 70 72 74 76 78 7a 7c 7e 80 82 84 86 88 8a
  //   8c 8e 90 92 94 96 98 9a 9c 9e a0 a2 a4 a6 a8 aa ac ae b0 b2 b4 b6 b8 ba bc be c0 c2 c4 c6 c8 ca cc
  //   ce d0 d2 d4 d6 d8 da dc de e0 e2 e4 e6 e8 ea ec ee f0 f2 f4 f6 f8 fa fc 2 4 2 4 2 4 2 4 2 4 2 4 2 4
  //   2 4 2 4 2 4 2 4 2 4 2 4 2 4 2 4 3 5 2 4 2 4 2 4 2 4 2 4 2 4 2 4 3 5 2 4 2 4 2 4 3 5 2 4 3 5 3 5 3 5
  //   2 4 2 4 2 4 2 4 2 4 2 4 2 4 3 5 2 4 2 4 2 4 3 5 2 4 3 5 3 5 3 5 2 4 2 4 2 4 3 5 2 4 3 5 3 5 3 5 2 4
  //   3 5 3 5 3 5 3 5 3 5 3 5 3 5
endmodule

module Combinational (
  input  In7,
  input  In6,
  input  In5,
  input  In4,
  input  In3,
  input  In2,
  input  In1,
  input  In0,
  output Out2,
  output [2:0] Out,
  output Out1,
  output Out0
);

  wire and_1_out, and_2_out, and_3_out, and_4_out, and_5_out, and_6_out, and_7_out, and_8_out, and_9_out,
       and_10_out, and_11_out, not_1_out, not_2_out, not_3_out, not_4_out, not_5_out, not_6_out, not_7_out,
       not_8_out, not_9_out, not_10_out, not_11_out, not_12_out, not_13_out, not_14_out, not_15_out,
       not_16_out, not_17_out, not_18_out, not_19_out, not_20_out, not_21_out, not_22_out, not_23_out,
       not_24_out, not_25_out, not_26_out, not_27_out, not_28_out, not_29_out, not_30_out, not_31_out,
       not_32_out, not_33_out, not_34_out, not_35_out, not_36_out, not_37_out, not_38_out, not_39_out,
       not_40_out, not_41_out, not_42_out, not_43_out, not_44_out, not_45_out, not_46_out, not_47_out,
       not_48_out, not_49_out, not_50_out, not_51_out;

  not not_1 (not_1_out, In7);
  not not_2 (not_2_out, In6);
  not not_3 (not_3_out, In5);
  not not_4 (not_4_out, In4);
  not not_5 (not_5_out, In3);
  not not_6 (not_6_out, In2);
  not not_7 (not_7_out, In7);
  not not_8 (not_8_out, In6);
  not not_9 (not_9_out, In5);
  not not_10 (not_10_out, In4);
  not not_11 (not_11_out, In3);
  not not_12 (not_12_out, In7);
  not not_13 (not_13_out, In6);
  not not_14 (not_14_out, In5);
  not not_15 (not_15_out, In4);
  not not_16 (not_16_out, In3);
  not not_17 (not_17_out, In1);
  not not_18 (not_18_out, In0);
  not not_19 (not_19_out, In7);
  not not_20 (not_20_out, In6);
  not not_21 (not_21_out, In5);
  not not_22 (not_22_out, In4);
  not not_23 (not_23_out, In2);
  not not_24 (not_24_out, In0);
  not not_25 (not_25_out, In7);
  not not_26 (not_26_out, In6);
  not not_27 (not_27_out, In5);
  not not_28 (not_28_out, In4);
  not not_29 (not_29_out, In3);
  not not_30 (not_30_out, In1);
  not not_31 (not_31_out, In7);
  not not_32 (not_32_out, In6);
  not not_33 (not_33_out, In5);
  not not_34 (not_34_out, In4);
  not not_35 (not_35_out, In3);
  not not_36 (not_36_out, In0);
  not not_37 (not_37_out, In5);
  not not_38 (not_38_out, In7);
  not not_39 (not_39_out, In5);
  not not_40 (not_40_out, In4);
  not not_41 (not_41_out, In3);
  not not_42 (not_42_out, In1);
  not not_43 (not_43_out, In7);
  not not_44 (not_44_out, In5);
  not not_45 (not_45_out, In4);
  not not_46 (not_46_out, In2);
  not not_47 (not_47_out, In0);
  not not_48 (not_48_out, In7);
  not not_49 (not_49_out, In5);
  not not_50 (not_50_out, In4);
  not not_51 (not_51_out, In5);
  and and_1 (and_1_out, not_1_out, not_2_out, not_3_out, not_4_out, not_5_out, not_6_out, In0);
  and and_2 (and_2_out, not_7_out, not_8_out, not_9_out, not_10_out, not_11_out, In1, In0);
  and and_3 (and_3_out, not_12_out, not_13_out, not_14_out, not_15_out, not_16_out, In2, not_17_out, not_18_out);
  and and_4 (and_4_out, not_19_out, not_20_out, not_21_out, not_22_out, In3, not_23_out, In1, not_24_out);
  and and_5 (and_5_out, not_25_out, not_26_out, not_27_out, not_28_out, not_29_out, not_30_out, In0);
  and and_6 (and_6_out, not_31_out, not_32_out, not_33_out, not_34_out, not_35_out, In2, not_36_out);
  and and_7 (and_7_out, In7, In6, not_37_out);
  and and_8 (and_8_out, not_38_out, not_39_out, not_40_out, not_41_out, not_42_out, In0);
  and and_9 (and_9_out, not_43_out, not_44_out, not_45_out, not_46_out, In1, not_47_out);
  and and_10 (and_10_out, not_48_out, In6, not_49_out, not_50_out);
  and and_11 (and_11_out, In7, In6, not_51_out, In4);
  or or_1 (Out[2], and_1_out, and_2_out, and_3_out, and_4_out);
  or or_2 (Out[1], and_5_out, and_6_out, and_7_out);
  or or_3 (Out[0], and_8_out, and_9_out, and_10_out, and_11_out);

  assign Out0 = Out[0];
  assign Out1 = Out[1];
  assign Out2 = Out[2];
endmodule
