// Logisim project Lab 3 Given.circ as structural Verilog: 8 circuits, main circuit Main
module Main (
  input  in_1
);

  wire ALUOp0, ALUOp1, ALUSrcA, ALUSrcB0, ALUSrcB1, and_2_out, and_3_out, and_4_out, and_5_out, and_6_out,
       CLK, IorD, IrWrite, M2Reg0, M2Reg1, MemRead, MemWrite, not_1_out, not_2_out, PCEn, PCN, PCSour0,
       PCSour1, PCWrite, PCWriteCond, RegDist0, RegDist1, RegWrite, Zero, ZImm;
  wire [2:0] alucontrol_1_out0;
  wire [4:0] multiplexer_3_out, Reg1, Reg2, Shamt;
  wire [5:0] Func, OpCode;
  wire [6:0] bit_extender_1_out, bit_extender_2_out;
  wire [7:0] multiplexer_1_out;
  wire [15:11] IR_q;
  wire [31:0] ALUOut, ALURes, B, bit_extender_3_out, bit_extender_4_out, bit_extender_5_out, MDR_q,
       multiplexer_2_out, multiplexer_4_out, multiplexer_7_out, PC, PCNew, ram_1_data, RD2, RegA,
       register_file_2_rddata1, register_file_2_rddata2, shifter_1_out, shifter_2_out;
  wire [31:26] adder_1_out, undriven;

  // AND_Gate and_1 has open pins: in0=PCN, in1=PCEn, out=open
  Register #(.width(32)) u_PC (.D(PCNew), .en(PCEn), .Q(PC), .clk(CLK));  // open: clr
  and and_2 (and_2_out, Zero, PCWriteCond);
  or or_1 (PCEn, and_2_out, PCWrite);
  Register_File register_file_1 ();  // open: WrAddr, WrData, WrReg, RdAddr1, RdAddr2, RdData1, RdData2, Clock
  and and_3 (and_3_out, PCSour0, PCSour1);
  // Probe on PC
  Bit_Extender #(.in_width(32), .out_width(7)) bit_extender_1 (.in(PC), .out(bit_extender_1_out));
  ALU alu_1 ();  // open: ALUCtl, A, B, ALUResult, Zero, Overflow, Shamt
  // Probe on and_3_out
  // Probe on RegWrite
  Bit_Extender #(.in_width(32), .out_width(7)) bit_extender_2 (.in(ALUOut), .out(bit_extender_2_out));
  Counter #(.width(1), .max('h1), .ongoal("stay")) counter_1 (.carry(PCN), .clk(PCEn));  // open: load, D, count, Q, clr
  // Probe on MemWrite
  Clock clock_1 (.out(CLK));
  Multiplexer #(.width(8), .enable("false")) multiplexer_1 (
    .in0({1'b0, bit_extender_1_out}), .in1({1'b1, bit_extender_2_out}), .out(multiplexer_1_out), .sel(IorD));
  not not_1 (not_1_out, ALUSrcB1);
  not not_2 (not_2_out, ALUSrcB0);
  // Probe on RD2
  and and_4 (and_4_out, PCWrite, PCSour1);
  // Probe on and_4_out
  and and_5 (and_5_out, PCWrite, PCSour1, RegDist1, M2Reg1, RegWrite);
  // Probe on and_5_out
  RAM #(.dataWidth(32), .bus("separate")) ram_1 (
    .addr(multiplexer_1_out), .din(RD2), .data(ram_1_data), .str(MemWrite), .clk(CLK), .ld(MemRead));  // open: sel, clr
  and and_6 (and_6_out, ALUSrcA, ALUOp0, PCWriteCond, PCSour0, not_1_out, not_2_out);
  // Probe on and_6_out
  Adder #(.width(6)) adder_1 (.a(undriven), .b(6'b000001), .out(adder_1_out));  // open: cin, cout
  Register #(.width(32)) IR (
    .D(ram_1_data), .en(IrWrite), .Q({OpCode, Reg1, Reg2, IR_q, Shamt, Func}), .clk(CLK));  // open: clr
  Register #(.width(32)) MDR (.D(ram_1_data), .Q(MDR_q), .clk(CLK));  // open: en, clr
  Multiplexer #(.select(2), .width(32), .enable("false")) multiplexer_2 (
    .in0(ALUOut), .in1(MDR_q), .in2(PC), .out(multiplexer_2_out), .sel({M2Reg1, M2Reg0}));  // open: in3
  ControlUnit controlunit_1 (
    .Opcode(OpCode), .PCWrite(PCWrite), .PCWriteCond(PCWriteCond), .IorD(IorD), .MemRead(MemRead),
    .MemWrite(MemWrite), .IrWrite(IrWrite), .M2Reg1(M2Reg1), .M2Reg0(M2Reg0), .CLK(CLK), .RegDst0(RegDist0),
    .RegDst1(RegDist1), .RegWrite(RegWrite), .ALUSrcA(ALUSrcA), .ALUSrcB0(ALUSrcB0), .ALUSrcB1(ALUSrcB1),
    .ALUOp0(ALUOp0), .ALUOp1(ALUOp1), .ZImm(ZImm), .Func(Func), .PCSour1(PCSour1), .PCSour0(PCSour0));
  assign bit_extender_3_out = {{16{IR_q[15]}}, {IR_q, Shamt, Func}};  // Bit_Extender bit_extender_3
  assign bit_extender_4_out = {{16{1'b0}}, {IR_q, Shamt, Func}};  // Bit_Extender bit_extender_4
  Multiplexer #(.select(2), .width(5), .enable("false")) multiplexer_3 (
    .in0(Reg2), .in1(IR_q), .in2({5{1'b1}}), .out(multiplexer_3_out), .sel({RegDist1, RegDist0}));  // open: in3
  assign bit_extender_5_out = {{6{Reg1[4]}}, {Reg1, Reg2, IR_q, Shamt, Func}};  // Bit_Extender bit_extender_5
  Multiplexer #(.width(32), .enable("false")) multiplexer_4 (
    .in0(bit_extender_3_out), .in1(bit_extender_4_out), .out(multiplexer_4_out), .sel(ZImm));
  Shifter #(.width(32)) shifter_1 (.in(bit_extender_5_out), .\dist (5'b00010), .out(shifter_1_out));
  Shifter #(.width(32)) shifter_2 (.in(multiplexer_4_out), .\dist (5'b00010), .out(shifter_2_out));
  // Probe on multiplexer_2_out
  // Probe on multiplexer_3_out
  Register_File register_file_2 (
    .WrAddr(multiplexer_3_out), .WrData(multiplexer_2_out), .WrReg(RegWrite), .RdAddr1(Reg1), .RdAddr2(Reg2),
    .RdData1(register_file_2_rddata1), .RdData2(register_file_2_rddata2), .Clock(CLK));
  Multiplexer #(.select(2), .width(32)) multiplexer_5 (
    .in0(RD2), .in1(32'h4), .in2(multiplexer_4_out), .in3(shifter_2_out), .out(B), .sel({ALUSrcB1, ALUSrcB0}));  // open: en
  Multiplexer #(.select(2), .width(32), .enable("false")) multiplexer_6 (
    .in0(ALURes), .in1(ALUOut), .in2(shifter_1_out), .in3(RegA), .out(PCNew), .sel({PCSour1, PCSour0}));
  Register #(.width(32)) A (.D(register_file_2_rddata1), .Q(RegA), .clk(CLK));  // open: en, clr
  Register #(.width(32)) u_B (.D(register_file_2_rddata2), .Q(RD2), .clk(CLK));  // open: en, clr
  Multiplexer #(.width(32), .enable("false")) multiplexer_7 (
    .in0(PC), .in1(RegA), .out(multiplexer_7_out), .sel(ALUSrcA));
  ALUControl alucontrol_1 (
    .Op5(OpCode[5]), .Op4(OpCode[4]), .Op3(OpCode[3]), .Op2(OpCode[2]), .Op1(OpCode[1]), .Op0(OpCode[0]),
    .Func5(Func[5]), .Func4(Func[4]), .Func3(Func[3]), .Func2(Func[2]), .Func1(Func[1]), .Func0(Func[0]),
    .Out2(alucontrol_1_out0[2]), .Out1(alucontrol_1_out0[1]), .Out0(alucontrol_1_out0[0]));
  ALU alu_2 (
    .ALUCtl(alucontrol_1_out0), .A(multiplexer_7_out), .B(B), .ALUResult(ALURes), .Zero(Zero), .Shamt(Shamt));  // open: Overflow
  // Probe on B
  Register #(.width(32)) u_ALUOut (.D(ALURes), .Q(ALUOut), .clk(CLK));  // open: en, clr
endmodule

module ALU (
  input  [2:0] ALUCtl,
  input  [31:0] A,
  input  [31:0] B,
  input  [4:0] Shamt,
  output [31:0] ALUResult,
  output Zero,
  output Overflow
);

  wire comparator_1_lt, comparator_2_lt, comparator_3_eq, comparator_4_eq, or_2_out;
  wire [31:0] ADD, AND, NOR, OR, SLL, SLT, SLTU, SRL, SUB, XOR;

  // Probe on ALUCtl
  assign NOR = ~(A | B);  // NOR_Gate nor_1, 32 bits wide
  Adder #(.width(32)) adder_1 (.a(A), .b(B), .out(ADD));  // open: cin, cout
  Subtractor #(.width(32)) subtractor_1 (.a(A), .b(B), .out(SUB));  // open: bin, bout
  assign AND = A & B;  // AND_Gate and_1, 32 bits wide
  assign OR = A | B;  // OR_Gate or_1, 32 bits wide
  assign XOR = A ^ B;  // XOR_Gate xor_1, 32 bits wide
  Comparator #(.width(32)) comparator_1 (.a(A), .b(B), .lt(comparator_1_lt));  // open: gt, eq
  assign SLT = {{31{1'b0}}, comparator_1_lt};  // Bit_Extender bit_extender_1
  Shifter #(.width(32)) shifter_1 (.in(B), .\dist (Shamt), .out(SLL));
  Shifter #(.width(32), .shift("lr")) shifter_2 (.in(B), .\dist (Shamt), .out(SRL));
  Comparator #(.width(32), .mode("unsigned")) comparator_2 (.a(A), .b(B), .lt(comparator_2_lt));  // open: gt, eq
  assign SLTU = {{31{1'b0}}, comparator_2_lt};  // Bit_Extender bit_extender_2
  Multiplexer #(.select(3), .width(32), .enable("false")) multiplexer_1 (
    .in0(NOR), .in1(AND), .in2(SUB), .in3(SLT), .in4(OR), .in5(ADD), .in6(SLL), .in7(SRL), .out(ALUResult),
    .sel(ALUCtl));
  Comparator #(.width(3)) comparator_3 (.a(3'b101), .b(ALUCtl), .eq(comparator_3_eq));  // open: gt, lt
  Comparator #(.width(3)) comparator_4 (.a(ALUCtl), .b(3'b010), .eq(comparator_4_eq));  // open: gt, lt
  Overflow_Unit overflow_unit_1 (
    .Add(comparator_3_eq), .Sub(comparator_4_eq), .ASign(A[31]), .BSign(B[31]), .ResultSign(ALUResult[31]),
    .Overflow(Overflow));
  not not_1 (Zero, or_2_out);
  or or_2 (or_2_out, ALUResult[0], ALUResult[1], ALUResult[2], ALUResult[3], ALUResult[4], ALUResult[5], ALUResult[6], ALUResult[7], ALUResult[8], ALUResult[9], ALUResult[10], ALUResult[11], ALUResult[12], ALUResult[13], ALUResult[14], ALUResult[15], ALUResult[16], ALUResult[17], ALUResult[18], ALUResult[19], ALUResult[20], ALUResult[21], ALUResult[22], ALUResult[23], ALUResult[24], ALUResult[25], ALUResult[26], ALUResult[27], ALUResult[28], ALUResult[29], ALUResult[30], ALUResult[31]);

  // Other names for the same wires on the sheet: ASign = A[31]; ResultSign = ALUResult[31]; BSign = B[31]

  // Notes on the sheet:
  //   ALUCtl for ADD for top port
  //   ALUCtl for SUB for second port
endmodule

module Register_File (
  input  [4:0] WrAddr,
  input  [31:0] WrData,
  input  WrReg,
  input  [4:0] RdAddr1,
  input  [4:0] RdAddr2,
  input  Clock,
  output [31:0] RdData1,
  output [31:0] RdData2
);

  wire WrReg0, WrReg1, WrReg2, WrReg3, WrReg4, WrReg5, WrReg6, WrReg7, WrReg8, WrReg9, WrReg10, WrReg11,
       WrReg12, WrReg13, WrReg14, WrReg15, WrReg16, WrReg17, WrReg18, WrReg19, WrReg20, WrReg21, WrReg22,
       WrReg23, WrReg24, WrReg25, WrReg26, WrReg27, WrReg28, WrReg29, WrReg30, WrReg31;
  wire [31:0] RegData1, RegData2, RegData3, RegData4, RegData5, RegData6, RegData7, RegData8, RegData9,
       RegData10, RegData11, RegData12, RegData13, RegData14, RegData15, RegData16, RegData17, RegData18,
       RegData19, RegData20, RegData21, RegData22, RegData23, RegData24, RegData25, RegData26, RegData27,
       RegData28, RegData29, RegData30, RegData31;

  Demultiplexer #(.select(5), .enable("false")) demultiplexer_1 (
    .out0(WrReg0), .out1(WrReg1), .out2(WrReg2), .out3(WrReg3), .out4(WrReg4), .out5(WrReg5), .out6(WrReg6),
    .out7(WrReg7), .out8(WrReg8), .out9(WrReg9), .out10(WrReg10), .out11(WrReg11), .out12(WrReg12),
    .out13(WrReg13), .out14(WrReg14), .out15(WrReg15), .out16(WrReg16), .out17(WrReg17), .out18(WrReg18),
    .out19(WrReg19), .out20(WrReg20), .out21(WrReg21), .out22(WrReg22), .out23(WrReg23), .out24(WrReg24),
    .out25(WrReg25), .out26(WrReg26), .out27(WrReg27), .out28(WrReg28), .out29(WrReg29), .out30(WrReg30),
    .out31(WrReg31), .in(WrReg), .sel(WrAddr));
  // Probe on RegData4
  Register #(.width(32)) Reg4 (.D(WrData), .en(WrReg4), .Q(RegData4), .clk(Clock));  // open: clr
  // Probe on RegData8
  Register #(.width(32)) Reg8 (.D(WrData), .en(WrReg8), .Q(RegData8), .clk(Clock));  // open: clr
  // Probe on RegData12
  Register #(.width(32)) Reg12 (.D(WrData), .en(WrReg12), .Q(RegData12), .clk(Clock));  // open: clr
  // Probe on RegData16
  Register #(.width(32)) Reg16 (.D(WrData), .en(WrReg16), .Q(RegData16), .clk(Clock));  // open: clr
  // Probe on RegData20
  Register #(.width(32)) Reg20 (.D(WrData), .en(WrReg20), .Q(RegData20), .clk(Clock));  // open: clr
  // Probe on RegData24
  Register #(.width(32)) Reg24 (.D(WrData), .en(WrReg24), .Q(RegData24), .clk(Clock));  // open: clr
  // Probe on RegData28
  Register #(.width(32)) Reg28 (.D(WrData), .en(WrReg28), .Q(RegData28), .clk(Clock));  // open: clr
  Register #(.width(32)) Reg1 (.D(WrData), .en(WrReg1), .Q(RegData1), .clk(Clock));  // open: clr
  Register #(.width(32)) Reg5 (.D(WrData), .en(WrReg5), .Q(RegData5), .clk(Clock));  // open: clr
  Register #(.width(32)) Reg9 (.D(WrData), .en(WrReg9), .Q(RegData9), .clk(Clock));  // open: clr
  Register #(.width(32)) Reg13 (.D(WrData), .en(WrReg13), .Q(RegData13), .clk(Clock));  // open: clr
  Register #(.width(32)) Reg17 (.D(WrData), .en(WrReg17), .Q(RegData17), .clk(Clock));  // open: clr
  Register #(.width(32)) Reg21 (.D(WrData), .en(WrReg21), .Q(RegData21), .clk(Clock));  // open: clr
  Register #(.width(32)) Reg25 (.D(WrData), .en(WrReg25), .Q(RegData25), .clk(Clock));  // open: clr
  Register #(.width(32)) Reg29 (.D(WrData), .en(WrReg29), .Q(RegData29), .clk(Clock));  // open: clr
  // Probe on RegData1
  // Probe on RegData5
  // Probe on RegData9
  // Probe on RegData13
  // Probe on RegData17
  // Probe on RegData21
  // Probe on RegData25
  // Probe on RegData29
  // Probe on RegData2
  Register #(.width(32)) Reg2 (.D(WrData), .en(WrReg2), .Q(RegData2), .clk(Clock));  // open: clr
  // Probe on RegData6
  Register #(.width(32)) Reg6 (.D(WrData), .en(WrReg6), .Q(RegData6), .clk(Clock));  // open: clr
  // Probe on RegData10
  Register #(.width(32)) Reg10 (.D(WrData), .en(WrReg10), .Q(RegData10), .clk(Clock));  // open: clr
  // Probe on RegData14
  Register #(.width(32)) Reg14 (.D(WrData), .en(WrReg14), .Q(RegData14), .clk(Clock));  // open: clr
  // Probe on RegData18
  Register #(.width(32)) Reg18 (.D(WrData), .en(WrReg18), .Q(RegData18), .clk(Clock));  // open: clr
  // Probe on RegData22
  Register #(.width(32)) Reg22 (.D(WrData), .en(WrReg22), .Q(RegData22), .clk(Clock));  // open: clr
  // Probe on RegData26
  Register #(.width(32)) Reg26 (.D(WrData), .en(WrReg26), .Q(RegData26), .clk(Clock));  // open: clr
  // Probe on RegData30
  Register #(.width(32)) Reg30 (.D(WrData), .en(WrReg30), .Q(RegData30), .clk(Clock));  // open: clr
  // Probe on RegData3
  Register #(.width(32)) Reg3 (.D(WrData), .en(WrReg3), .Q(RegData3), .clk(Clock));  // open: clr
  // Probe on RegData7
  Register #(.width(32)) Reg7 (.D(WrData), .en(WrReg7), .Q(RegData7), .clk(Clock));  // open: clr
  // Probe on RegData11
  Register #(.width(32)) Reg11 (.D(WrData), .en(WrReg11), .Q(RegData11), .clk(Clock));  // open: clr
  // Probe on RegData15
  Register #(.width(32)) Reg15 (.D(WrData), .en(WrReg15), .Q(RegData15), .clk(Clock));  // open: clr
  // Probe on RegData19
  Register #(.width(32)) Reg19 (.D(WrData), .en(WrReg19), .Q(RegData19), .clk(Clock));  // open: clr
  // Probe on RegData23
  Register #(.width(32)) Reg23 (.D(WrData), .en(WrReg23), .Q(RegData23), .clk(Clock));  // open: clr
  // Probe on RegData27
  Register #(.width(32)) Reg27 (.D(WrData), .en(WrReg27), .Q(RegData27), .clk(Clock));  // open: clr
  // Probe on RegData31
  Register #(.width(32)) Reg31 (.D(WrData), .en(WrReg31), .Q(RegData31), .clk(Clock));  // open: clr
  Multiplexer #(.select(5), .width(32), .enable("false")) multiplexer_1 (
    .in0({32{1'b0}}), .in1(RegData1), .in2(RegData2), .in3(RegData3), .in4(RegData4), .in5(RegData5),
    .in6(RegData6), .in7(RegData7), .in8(RegData8), .in9(RegData9), .in10(RegData10), .in11(RegData11),
    .in12(RegData12), .in13(RegData13), .in14(RegData14), .in15(RegData15), .in16(RegData16),
    .in17(RegData17), .in18(RegData18), .in19(RegData19), .in20(RegData20), .in21(RegData21),
    .in22(RegData22), .in23(RegData23), .in24(RegData24), .in25(RegData25), .in26(RegData26),
    .in27(RegData27), .in28(RegData28), .in29(RegData29), .in30(RegData30), .in31(RegData31), .out(RdData1),
    .sel(RdAddr1));
  Multiplexer #(.select(5), .width(32), .enable("false")) multiplexer_2 (
    .in0({32{1'b0}}), .in1(RegData1), .in2(RegData2), .in3(RegData3), .in4(RegData4), .in5(RegData5),
    .in6(RegData6), .in7(RegData7), .in8(RegData8), .in9(RegData9), .in10(RegData10), .in11(RegData11),
    .in12(RegData12), .in13(RegData13), .in14(RegData14), .in15(RegData15), .in16(RegData16),
    .in17(RegData17), .in18(RegData18), .in19(RegData19), .in20(RegData20), .in21(RegData21),
    .in22(RegData22), .in23(RegData23), .in24(RegData24), .in25(RegData25), .in26(RegData26),
    .in27(RegData27), .in28(RegData28), .in29(RegData29), .in30(RegData30), .in31(RegData31), .out(RdData2),
    .sel(RdAddr2));
endmodule

module Overflow_Unit (
  input  Add,
  input  Sub,
  input  ASign,
  input  BSign,
  input  ResultSign,
  output Overflow
);

  wire and_1_out, and_2_out, or_1_out, xnor_1_out, xor_1_out, xor_2_out;

  xnor xnor_1 (xnor_1_out, ASign, BSign);
  xor xor_1 (xor_1_out, ASign, BSign);
  and and_1 (and_1_out, xnor_1_out, Add);
  and and_2 (and_2_out, xor_1_out, Sub);
  or or_1 (or_1_out, and_1_out, and_2_out);
  xor xor_2 (xor_2_out, ResultSign, ASign);
  and and_3 (Overflow, or_1_out, xor_2_out);

  // Notes on the sheet:
  //   Overflow occurs when doing addition and sign(A) == sign(B) && sign(result) != sign(A)
  //   Or
  //   Overflow occurs when doing subtraction and sign(A) != sign(B) && sign(result) != sign(A)
endmodule

module ControlUnit (
  input  [5:0] Opcode,
  input  CLK,
  input  [5:0] Func,
  output PCWrite,
  output IorD,
  output PCWriteCond,
  output MemRead,
  output MemWrite,
  output IrWrite,
  output M2Reg1,
  output M2Reg0,
  output PCSour1,
  output PCSour0,
  output ALUOp1,
  output ALUOp0,
  output ALUSrcB1,
  output ALUSrcB0,
  output ALUSrcA,
  output RegWrite,
  output RegDst1,
  output RegDst0,
  output ZImm
);

  wire and_1_out, PCSour0_t, PCSour1_t;
  wire [3:0] register_1_q, rom_1_data;

  ROM #(.addrWidth(10), .dataWidth(4)) rom_1 (.addr({Opcode, register_1_q}), .data(rom_1_data));  // open: sel
  Register #(.width(4), .trigger("falling")) register_1 (.D(rom_1_data), .Q(register_1_q), .clk(CLK));  // open: en, clr
  ROM #(.addrWidth(4), .dataWidth(19)) rom_2 ();  // open: addr, data, sel
  ROM #(.addrWidth(10), .dataWidth(4)) rom_3 ();  // open: addr, data, sel
  ROM #(.addrWidth(4), .dataWidth(19)) rom_4 (
    .addr(register_1_q),
    .data({ZImm, RegDst0, RegDst1, RegWrite, ALUSrcA, ALUSrcB0, ALUSrcB1, ALUOp0, ALUOp1, PCSour0_t, PCSour1_t, M2Reg0, M2Reg1, IrWrite, MemWrite, MemRead, IorD, PCWriteCond, PCWrite}));  // open: sel
  and and_1 (and_1_out, Func[3], 1'b1);
  or or_1 (PCSour1, PCSour1_t, and_1_out);
  or or_2 (PCSour0, and_1_out, PCSour0_t);

  // Notes on the sheet:
  //   contents of rom_1 (hex, n*v repeats v):
  //   1 6 0 4 0 0 7 4*0 e e e 18*0 1 9 0 4 0 0 7 4*0 e e e 0 0 0 a 14*0 1 8 0 4 0 0 7 4*0 e e e 18*0 1 0 0
  //   4 0 0 7 4*0 e e e 18*0 1 b 0 4 0 0 7 4*0 e e e 18*0 1 0 0 4 0 0 7 4*0 e e e 18*0 1 c 0 4 0 0 7 4*0 e
  //   e e 0 0 0 d 14*0 1 0 0 4 0 0 7 4*0 e e e 18*0 1 0 0 4 0 0 7 4*0 e e e 18*0 1 0 0 4 0 0 7 4*0 e e e
  //   18*0 1 0 0 4 0 0 7 4*0 e e e 18*0 1 0 0 4 0 0 7 4*0 e e e 18*0 1 0 0 4 0 0 7 4*0 e e e 18*0 1 0 0 4
  //   0 0 7 4*0 e e e 18*0 1 0 0 4 0 0 7 4*0 e e e 18*0 1 0 0 4 0 0 7 4*0 e e e 18*0 1 0 0 4 0 0 7 4*0 e e
  //   e 18*0 1 0 0 4 0 0 7 4*0 e e e 0 0 0 2 3 13*0 1 0 0 4 0 0 7 4*0 e e e 18*0 1 0 0 4 0 0 7 4*0 e e e
  //   18*0 1 0 0 4 0 0 7 4*0 e e e 18*0 1 0 0 4 0 0 7 4*0 e e e 0 0 0 2 5 13*0 1 0 0 4 0 0 7 4*0 e e e
  //   18*0 1 0 0 4 0 0 7 4*0 e e e 18*0 1 0 0 4 0 0 7 4*0 e e e 18*0 1 0 0 4 0 0 7 4*0 e e e 18*0 1 0 0 4
  //   0 0 7 4*0 e e e 18*0 1 0 0 4 0 0 7 4*0 e e e 18*0 1 0 0 4 0 0 7 4*0 e e e 18*0 1 0 0 4 0 0 7 4*0 e e
  //   e 18*0 1 0 0 4 0 0 7 4*0 e e e 18*0 1 0 0 4 0 0 7 4*0 e e e
  //   contents of rom_2 (hex, n*v repeats v):
  //   0 2029 3000 5000 c 78080 14 4400 28000 4a02 101 10141 5000 45000 45000 8000
  //   contents of rom_3 (hex, n*v repeats v):
  //   1 2 7 0 5 0 0 8 4*0 f f f 17*0 1 2 a 0 5 0 0 8 4*0 f f f 0 0 0 a 13*0 1 2 9 0 5 0 0 8 4*0 f f f 17*0
  //   1 2 0 0 5 0 0 8 4*0 f f f 17*0 1 2 c 0 5 0 0 8 4*0 f f f 17*0 1 2 0 0 5 0 0 8 4*0 f f f 17*0 1 2 d 0
  //   5 0 0 8 4*0 f f f 0 0 0 d 13*0 1 2 0 0 5 0 0 8 4*0 f f f 17*0 1 2 0 0 5 0 0 8 4*0 f f f 17*0 1 2 0 0
  //   5 0 0 8 4*0 f f f 17*0 1 2 0 0 5 0 0 8 4*0 f f f 17*0 1 2 0 0 5 0 0 8 4*0 f f f 17*0 1 2 0 0 5 0 0 8
  //   4*0 f f f 17*0 1 2 0 0 5 0 0 8 4*0 f f f 17*0 1 2 0 0 5 0 0 8 4*0 f f f 17*0 1 2 0 0 5 0 0 8 4*0 f f
  //   f 17*0 1 2 0 0 5 0 0 8 4*0 f f f 17*0 1 2 0 0 5 0 0 8 4*0 f f f 0 0 0 3 4 12*0 1 2 0 0 5 0 0 8 4*0 f
  //   f f 17*0 1 2 0 0 5 0 0 8 4*0 f f f 17*0 1 2 0 0 5 0 0 8 4*0 f f f 17*0 1 2 0 0 5 0 0 8 4*0 f f f 0 0
  //   0 3 6 12*0 1 2 0 0 5 0 0 8 4*0 f f f 17*0 1 2 0 0 5 0 0 8 4*0 f f f 17*0 1 2 0 0 5 0 0 8 4*0 f f f
  //   17*0 1 2 0 0 5 0 0 8 4*0 f f f 17*0 1 2 0 0 5 0 0 8 4*0 f f f 17*0 1 2 0 0 5 0 0 8 4*0 f f f 17*0 1
  //   2 0 0 5 0 0 8 4*0 f f f 17*0 1 2 0 0 5 0 0 8 4*0 f f f 17*0 1 2 0 0 5 0 0 8 4*0 f f f 17*0 1 2 0 0 5
  //   0 0 8 4*0 f f f
  //   contents of rom_4 (hex, n*v repeats v):
  //   2029 3000 5000 c 78080 14 4400 28000 4a02 101 10141 5000 45000 45000 8000
endmodule

// ALUCon
module ALUControl (
  input  Op5,
  input  Op4,
  input  Op3,
  input  Op2,
  input  Op1,
  input  Op0,
  input  Func5,
  input  Func4,
  input  Func3,
  input  Func2,
  input  Func1,
  input  Func0,
  output Out2,
  output Out1,
  output Out0
);

  wire and_1_out, and_2_out, and_3_out, and_4_out, and_5_out, and_6_out, and_7_out, and_8_out, not_1_out,
       not_2_out, not_3_out, not_4_out, not_5_out, not_6_out, not_7_out, not_8_out, not_9_out, not_10_out,
       not_11_out, not_12_out, not_13_out, not_14_out, not_15_out;

  not not_1 (not_1_out, Op2);
  not not_2 (not_2_out, Func2);
  and and_1 (and_1_out, not_1_out, not_2_out, not_3_out);
  not not_3 (not_3_out, Func1);
  not not_4 (not_4_out, Op2);
  and and_2 (and_2_out, not_4_out, not_5_out, Func0);
  not not_5 (not_5_out, Func1);
  and and_3 (and_3_out, Op3, not_6_out);
  not not_6 (not_6_out, Op2);
  not not_7 (not_7_out, Op5);
  not not_8 (not_8_out, Op3);
  not not_9 (not_9_out, Func2);
  not not_10 (not_10_out, Op3);
  not not_11 (not_11_out, Op2);
  and and_4 (and_4_out, not_11_out, not_12_out, not_13_out);
  not not_12 (not_12_out, Func1);
  not not_13 (not_13_out, Func0);
  not not_14 (not_14_out, Op2);
  and and_5 (and_5_out, not_14_out, Func3);
  and and_6 (and_6_out, Op3, not_15_out);
  not not_15 (not_15_out, Op0);
  or or_1 (Out2, and_1_out, and_2_out, Op0, and_3_out);
  and and_7 (and_7_out, not_7_out, not_8_out, not_9_out, Func1);
  or or_2 (Out1, and_7_out, and_8_out);
  and and_8 (and_8_out, not_10_out, Op2);
  or or_3 (Out0, and_4_out, and_5_out, and_6_out, Op5);
endmodule

module Extra (
  input  [3:0] StateRegister,
  input  [3:0] StateRegister_2,
  input  [5:0] Opcode,
  input  in_4,
  input  CLK
);

  wire [3:0] register_1_q, rom_1_data;
  wire [17:0] rom_3_data;

  ROM #(.addrWidth(10), .dataWidth(4)) rom_1 (.addr({Opcode, register_1_q}), .data(rom_1_data), .sel(1'b1));
  Register #(.width(4)) register_1 (.D(rom_1_data), .Q(register_1_q), .clk(CLK));  // open: en, clr
  ROM #(.addrWidth(10), .dataWidth(4)) rom_2 ();  // open: addr, data, sel
  ROM #(.addrWidth(4), .dataWidth(18)) rom_3 (.addr(StateRegister_2), .data(rom_3_data), .sel(in_4));
  ROM #(.addrWidth(10), .dataWidth(4)) rom_4 ();  // open: addr, data, sel

  // Notes on the sheet:
  //   contents of rom_1 (hex, n*v repeats v):
  //   1 6 0 4 0 0 7 4*0 c 20*0 1 9 0 4 0 0 7 4*0 c 5*0 a 14*0 1 8 0 4 0 0 7 4*0 c 20*0 1 0 0 4 0 0 7 4*0 c
  //   20*0 1 b 0 4 0 0 7 4*0 c 20*0 1 0 0 4 0 0 7 4*0 c 20*0 1 c 0 4 0 0 7 4*0 c 5*0 d 14*0 1 0 0 4 0 0 7
  //   4*0 c 20*0 1 0 0 4 0 0 7 4*0 c 20*0 1 0 0 4 0 0 7 4*0 c 20*0 1 0 0 4 0 0 7 4*0 c 20*0 1 0 0 4 0 0 7
  //   4*0 c 20*0 1 0 0 4 0 0 7 4*0 c 20*0 1 0 0 4 0 0 7 4*0 c 20*0 1 0 0 4 0 0 7 4*0 c 20*0 1 0 0 4 0 0 7
  //   4*0 c 20*0 1 0 0 4 0 0 7 4*0 c 20*0 1 0 0 4 0 0 7 4*0 c 5*0 2 3 13*0 1 0 0 4 0 0 7 4*0 c 20*0 1 0 0
  //   4 0 0 7 4*0 c 20*0 1 0 0 4 0 0 7 4*0 c 20*0 1 0 0 4 0 0 7 4*0 c 5*0 2 5 13*0 1 0 0 4 0 0 7 4*0 c
  //   20*0 1 0 0 4 0 0 7 4*0 c 20*0 1 0 0 4 0 0 7 4*0 c 20*0 1 0 0 4 0 0 7 4*0 c 20*0 1 0 0 4 0 0 7 4*0 c
  //   20*0 1 0 0 4 0 0 7 4*0 c 20*0 1 0 0 4 0 0 7 4*0 c 20*0 1 0 0 4 0 0 7 4*0 c 20*0 1 0 0 4 0 0 7 4*0 c
  //   20*0 1 0 0 4 0 0 7 4*0 c
  //   contents of rom_2 (hex, n*v repeats v):
  //   1 6 0 4 0 0 7 4*0 c 20*0 1 9 0 4 0 0 7 4*0 c 5*0 a 14*0 1 8 0 4 0 0 7 4*0 c 20*0 1 0 0 4 0 0 7 4*0 c
  //   20*0 1 b 0 4 0 0 7 4*0 c 20*0 1 0 0 4 0 0 7 4*0 c 20*0 1 b 0 4 0 0 7 4*0 c 5*0 b 14*0 1 0 0 4 0 0 7
  //   4*0 c 20*0 1 0 0 4 0 0 7 4*0 c 20*0 1 0 0 4 0 0 7 4*0 c 20*0 1 0 0 4 0 0 7 4*0 c 20*0 1 0 0 4 0 0 7
  //   4*0 c 20*0 1 0 0 4 0 0 7 4*0 c 20*0 1 0 0 4 0 0 7 4*0 c 20*0 1 0 0 4 0 0 7 4*0 c 20*0 1 0 0 4 0 0 7
  //   4*0 c 20*0 1 0 0 4 0 0 7 4*0 c 20*0 1 0 0 4 0 0 7 4*0 c 5*0 2 3 13*0 1 0 0 4 0 0 7 4*0 c 20*0 1 0 0
  //   4 0 0 7 4*0 c 20*0 1 0 0 4 0 0 7 4*0 c 20*0 1 0 0 4 0 0 7 4*0 c 5*0 2 5 13*0 1 0 0 4 0 0 7 4*0 c
  //   20*0 1 0 0 4 0 0 7 4*0 c 20*0 1 0 0 4 0 0 7 4*0 c 20*0 1 0 0 4 0 0 7 4*0 c 20*0 1 0 0 4 0 0 7 4*0 c
  //   20*0 1 0 0 4 0 0 7 4*0 c 20*0 1 0 0 4 0 0 7 4*0 c 20*0 1 0 0 4 0 0 7 4*0 c 20*0 1 0 0 4 0 0 7 4*0 c
  //   20*0 1 0 0 4 0 0 7 4*0 c
  //   contents of rom_3 (hex, n*v repeats v):
  //   2029 3000 5000 c 38080 14 4400 28000 4a02 101 10141 5000 8000
  //   contents of rom_4 (hex, n*v repeats v):
  //   1 6 0 4 0 0 7 4*0 c 20*0 1 9 0 4 0 0 7 4*0 c 5*0 a 14*0 1 8 0 4 0 0 7 4*0 c 20*0 1 0 0 4 0 0 7 4*0 c
  //   20*0 1 b 0 4 0 0 7 4*0 c 20*0 1 0 0 4 0 0 7 4*0 c 20*0 1 b 0 4 0 0 7 4*0 c 5*0 b 14*0 1 0 0 4 0 0 7
  //   4*0 c 20*0 1 0 0 4 0 0 7 4*0 c 20*0 1 0 0 4 0 0 7 4*0 c 20*0 1 0 0 4 0 0 7 4*0 c 20*0 1 0 0 4 0 0 7
  //   4*0 c 20*0 1 0 0 4 0 0 7 4*0 c 20*0 1 0 0 4 0 0 7 4*0 c 20*0 1 0 0 4 0 0 7 4*0 c 20*0 1 0 0 4 0 0 7
  //   4*0 c 20*0 1 0 0 4 0 0 7 4*0 c 20*0 1 0 0 4 0 0 7 4*0 c 5*0 2 3 13*0 1 0 0 4 0 0 7 4*0 c 20*0 1 0 0
  //   4 0 0 7 4*0 c 20*0 1 0 0 4 0 0 7 4*0 c 20*0 1 0 0 4 0 0 7 4*0 c 5*0 2 5 13*0 1 0 0 4 0 0 7 4*0 c
  //   20*0 1 0 0 4 0 0 7 4*0 c 20*0 1 0 0 4 0 0 7 4*0 c 20*0 1 0 0 4 0 0 7 4*0 c 20*0 1 0 0 4 0 0 7 4*0 c
  //   20*0 1 0 0 4 0 0 7 4*0 c 20*0 1 0 0 4 0 0 7 4*0 c 20*0 1 0 0 4 0 0 7 4*0 c 20*0 1 0 0 4 0 0 7 4*0 c
  //   20*0 1 0 0 4 0 0 7 4*0 c
endmodule

module JR (
  input  [5:0] Func,
  output P1,
  output P0
);

  // AND_Gate and_1 has open pins: in0=Func[3], in1=1'b1, out=open
endmodule
