// Logisim project Lab 4 Given.circ as structural Verilog: 16 circuits, main circuit Main
module Main (
  output [1:0] out_1,
  output [1:0] out_2
);

  wire alu_1_zero, ALUSrc, Beq, BeqEX, Branch, BranchEX, BranchSuccess, CLK, ex_mem_1_memreadmem,
       ex_mem_1_memwritemem, FlushID, FlushIf, id_ex_1_alusrcex, JAL, JALEX, JALMEM, JR, JREX, Jump, JumpEX,
       mem_wb_1_isjalwb, mem_wb_1_memtoregwb, MemRead, MemReadEX, MemReg, MemRegEX, MemRegMEM, MemWrite,
       MemWriteEX, not_1_out, not_2_out, or_1_out, ReadRS, ReadRT, RegDst, RegWrite, RegWriteEX, RegWriteMEM,
       RegWriteWB, StallID, StallIF, Unsigned, xor_1_out;
  wire [2:0] ALUOP, id_ex_1_aluopex;
  wire [4:0] multiplexer_4_out, ShamtEX, WriteReg, WriteRegEX, WriteRegMEM, WriteRegWB;
  wire [5:0] Func, Opcode;
  wire [15:6] IMMI;
  wire [25:16] IMMJ;
  wire [27:0] PC_4;
  wire [31:0] adder_1_out, ALURes, bit_extender_2_out, bit_extender_3_out, BranchAddr, BubbleNum, data,
       ex_mem_1_aluresultmem, ex_mem_1_writedatamem, id_ex_1_immex, id_ex_1_pcplusex, ImmiExt, JumpAddrEX,
       JumpAddrMEM, mem_wb_1_aluresultwb, mem_wb_1_jumpaddrwb, mem_wb_1_readdatawb, multiplexer_1_out,
       multiplexer_2_out, multiplexer_3_out, multiplexer_7_out, multiplexer_8_out, multiplexer_9_out, PC_q,
       R2EX, ram_1_data, register_file_1_rddata1, register_file_1_rddata2, RIEX, rom_1_data, ShamtID,
       ShamtIDEX, shifter_1_out, WB, WBData;
  wire [31:28] JumpAddr;

  Clock clock_1 (.out(CLK));
  Multiplexer #(.width(32), .enable("false")) multiplexer_1 (
    .in0(multiplexer_2_out), .in1(RIEX), .out(multiplexer_1_out), .sel(JREX));
  // Probe on JREX
  Register #(.width(32)) PC (.D(multiplexer_1_out), .en(not_1_out), .Q(PC_q), .clk(CLK));  // open: clr
  not not_1 (not_1_out, StallIF);
  Multiplexer #(.width(32), .enable("false")) multiplexer_2 (
    .in0(multiplexer_3_out), .in1(JumpAddrEX), .out(multiplexer_2_out), .sel(JumpEX));
  // Probe on JumpEX
  Multiplexer #(.width(32), .enable("false")) multiplexer_3 (
    .in0(adder_1_out), .in1(BranchAddr), .out(multiplexer_3_out), .sel(BranchSuccess));
  // Probe on PC_q[9:2]
  Adder #(.width(32)) adder_1 (.a(PC_q), .b(32'h4), .out(adder_1_out));  // open: cin, cout
  // Probe on BranchSuccess
  ROM #(.dataWidth(32)) rom_1 (.addr(PC_q[9:2]), .data(rom_1_data));  // open: sel
  // Probe on rom_1_data
  not not_2 (not_2_out, StallID);
  IF_ID if_id_1 (
    .ADD(adder_1_out), .ROM(rom_1_data), .CLK(CLK), .ADDout({JumpAddr, PC_4}),
    .OUT({Opcode, IMMJ, IMMI, Func}), .clr(FlushIf), .en(not_2_out));
  // Probe on {Opcode, IMMJ, IMMI, Func}
  // Probe on IMMI[15:11]
  // Probe on IMMJ[20:16]
  // Probe on Opcode
  Control control_1 (
    .op(Opcode), .Funct(Func), .IsJAL(JAL), .MemRead(MemRead), .MemtoReg(MemReg), .MemWrite(MemWrite),
    .ALUop(ALUOP), .RegWrite(RegWrite), .Jump(Jump), .BneOrBeq(Beq), .Branch(Branch), .ALUSrc(ALUSrc),
    .RegDst(RegDst), .IsUnsigned(Unsigned), .JR(JR), .ReadRs(ReadRS), .ReadRt(ReadRT));
  Multiplexer #(.width(5), .enable("false")) multiplexer_4 (
    .in0(IMMJ[20:16]), .in1(IMMI[15:11]), .out(multiplexer_4_out), .sel(RegDst));
  assign ShamtID = {{27{IMMI[10]}}, IMMI[10:6]};  // Bit_Extender bit_extender_1
  assign bit_extender_2_out = {{16{IMMI[15]}}, {IMMI, Func}};  // Bit_Extender bit_extender_2
  assign bit_extender_3_out = {{16{1'b0}}, {IMMI, Func}};  // Bit_Extender bit_extender_3
  Multiplexer #(.width(5), .enable("false")) multiplexer_5 (
    .in0(multiplexer_4_out), .in1({5{1'b1}}), .out(WriteReg), .sel(JAL));
  Multiplexer #(.width(32), .enable("false")) multiplexer_6 (
    .in0(bit_extender_2_out), .in1(bit_extender_3_out), .out(ImmiExt), .sel(Unsigned));
  // Probe on WriteRegMEM
  // Probe on WriteRegEX
  or or_1 (or_1_out, JumpEX, JALEX, JREX, BranchSuccess);
  // Probe on IMMJ[25:21]
  // Probe on IMMJ[20:16]
  // Probe on WriteRegWB
  // Probe on WBData
  Register_File register_file_1 (
    .WrAddr(WriteRegWB), .WrData(WBData), .WrReg(RegWriteWB), .RdAddr1(IMMJ[25:21]), .RdAddr2(IMMJ[20:16]),
    .RdData1(register_file_1_rddata1), .RdData2(register_file_1_rddata2), .Clock(CLK));
  // Probe on RegWriteWB
  HazardUnit hazardunit_1 (
    .clk(CLK), .ReadRt(ReadRT), .ReadRs(ReadRS), .RegWriteMEM(RegWriteMEM), .RS(IMMJ[25:21]),
    .WriteReg_MEM(WriteRegMEM), .WriteReg_EX(WriteRegEX), .RT(IMMJ[20:16]), .RegWriteEX(RegWriteEX),
    .IsLW(MemReadEX), .RsOutput(out_1), .FlushID(FlushID), .StallIF(StallIF), .StallID(StallID),
    .BubbleNum(BubbleNum), .RtOutput(out_2), .FlushIF(FlushIf), .IsToBranchOrJump(or_1_out));
  // Probe on out_1
  // Probe on register_file_1_rddata1
  // Probe on register_file_1_rddata2
  Multiplexer #(.select(2), .width(32), .enable("false")) multiplexer_7 (
    .in0(register_file_1_rddata1), .in1(ALURes), .in2(data), .out(multiplexer_7_out), .sel(out_1));  // open: in3
  Multiplexer #(.select(2), .width(32), .enable("false")) multiplexer_8 (
    .in0(register_file_1_rddata2), .in1(ALURes), .in2(data), .out(multiplexer_8_out), .sel(out_2));  // open: in3
  // Probe on ALUOP
  // Probe on multiplexer_7_out
  // Probe on multiplexer_8_out
  // Probe on data
  // Probe on ALURes
  // Probe on out_2
  ID_EX id_ex_1 (
    .MemWriteID(MemWrite), .ImmID(ImmiExt), .ShamtID(ShamtID), .IsJALID(JAL), .JumpID(Jump),
    .R1ID(multiplexer_7_out), .JumpAddr({JumpAddr, IMMJ, IMMI, Func, 2'b00}), .BranchID(Branch),
    .MemtoRegID(MemReg), .IsJRID(JR), .RegWriteID(RegWrite), .R2ID(multiplexer_8_out),
    .PCPlus4ID({JumpAddr, PC_4}), .BeqID(Beq), .ALUopID(ALUOP), .ALUSrcID(ALUSrc), .WriteReg_ID(WriteReg),
    .MemReadID(MemRead), .MemWriteEX(MemWriteEX), .ImmEX(id_ex_1_immex), .ShamtEX(ShamtIDEX),
    .IsJALEX(JALEX), .JumpEX(JumpEX), .R1EX(RIEX), .JumpAddr_2(JumpAddrEX), .BranchEX(BranchEX),
    .MemtoRegEX(MemRegEX), .IsJREX(JREX), .RegWriteEX(RegWriteEX), .R2EX(R2EX), .PCPlusEX(id_ex_1_pcplusex),
    .BneOrBeqEX(BeqEX), .ALUopEX(id_ex_1_aluopex), .ALUSrcEX(id_ex_1_alusrcex), .WriteReg_EX(WriteRegEX),
    .MemReadEX(MemReadEX), .clk(CLK), .clr(FlushID), .En(1'b1), .Shamt(IMMI[10:6]), .ShamtEX_2(ShamtEX));
  Shifter #(.width(32)) shifter_1 (.in(id_ex_1_immex), .\dist (5'b00010), .out(shifter_1_out));
  // Probe on R2EX
  // Probe on id_ex_1_immex
  // Probe on RIEX
  Multiplexer #(.width(32), .enable("false")) multiplexer_9 (
    .in0(R2EX), .in1(id_ex_1_immex), .out(multiplexer_9_out), .sel(id_ex_1_alusrcex));
  Adder #(.width(32)) adder_2 (.a(id_ex_1_pcplusex), .b(shifter_1_out), .out(BranchAddr));  // open: cin, cout
  ALU alu_1 (
    .ALUCtl(id_ex_1_aluopex), .A(RIEX), .B(multiplexer_9_out), .ALUResult(ALURes), .Zero(alu_1_zero),
    .Shamt(ShamtEX));  // open: Overflow
  // Probe on multiplexer_9_out
  // Probe on id_ex_1_aluopex
  // Probe on id_ex_1_pcplusex
  and and_1 (BranchSuccess, BranchEX, xor_1_out);
  xor xor_1 (xor_1_out, alu_1_zero, BeqEX);
  // Probe on WriteRegEX
  // Probe on ALURes
  EX_MEM ex_mem_1 (
    .IsJALEX(JALEX), .ALUResultEX(ALURes), .MemtoRegEX(MemRegEX), .RegWriteEX(RegWriteEX),
    .WriteDataEX(R2EX), .JumpAddrEX(id_ex_1_pcplusex), .MemReadEX(MemReadEX), .MemWriteEX(MemWriteEX),
    .WriteReg_EX(WriteRegEX), .IsJALMEM(JALMEM), .ALUResultMEM(ex_mem_1_aluresultmem),
    .MemtoRegMEM(MemRegMEM), .RegWriteMEM(RegWriteMEM), .WriteDataMEM(ex_mem_1_writedatamem),
    .JumpAddrMEM(JumpAddrMEM), .MemReadMEM(ex_mem_1_memreadmem), .MemWriteMEM(ex_mem_1_memwritemem),
    .WriteReg_MEM(WriteRegMEM), .clk(CLK), .clr(1'b0), .En(1'b1), .ZeroEX(alu_1_zero));  // open: ZeroMEM
  // Probe on WriteRegMEM
  Multiplexer #(.width(32), .enable("false")) multiplexer_10 (
    .in0(ex_mem_1_aluresultmem), .in1(ram_1_data), .out(data), .sel(MemRegMEM));
  // Probe on ex_mem_1_writedatamem
  // Probe on ex_mem_1_aluresultmem
  RAM #(.dataWidth(32), .bus("separate")) ram_1 (
    .addr(ex_mem_1_aluresultmem[9:2]), .din(ex_mem_1_writedatamem), .data(ram_1_data),
    .str(ex_mem_1_memwritemem), .clk(CLK), .ld(ex_mem_1_memreadmem));  // open: sel, clr
  // Probe on ex_mem_1_memwritemem
  // Probe on ram_1_data
  // Probe on WriteRegMEM
  MEM_WB mem_wb_1 (
    .IsJALMEM(JALMEM), .ALUResultMEM(ex_mem_1_aluresultmem), .MemtoRegMEM(MemRegMEM),
    .RegWriteMEM(RegWriteMEM), .ReadDataMEM(JumpAddrMEM), .JumpAddrMEM(ram_1_data),
    .WriteReg_MEM(WriteRegMEM), .IsJALWB(mem_wb_1_isjalwb), .ALUResultWB(mem_wb_1_aluresultwb),
    .MemtoRegWB(mem_wb_1_memtoregwb), .RegWriteWB(RegWriteWB), .ReadDataWB(mem_wb_1_readdatawb),
    .JumpAddrWB(mem_wb_1_jumpaddrwb), .WriteReg_WB(WriteRegWB), .clk(CLK), .clr(1'b0), .En(1'b1));
  // Probe on WriteRegWB
  // Probe on WriteRegMEM
  // Probe on mem_wb_1_aluresultwb
  // Probe on mem_wb_1_readdatawb
  // Probe on mem_wb_1_jumpaddrwb
  Multiplexer #(.width(32), .enable("false")) multiplexer_11 (
    .in0(mem_wb_1_aluresultwb), .in1(mem_wb_1_jumpaddrwb), .out(WB), .sel(mem_wb_1_memtoregwb));
  // Probe on mem_wb_1_isjalwb
  // Probe on WBData
  Multiplexer #(.width(32), .enable("false")) multiplexer_12 (
    .in0(WB), .in1(mem_wb_1_readdatawb), .out(WBData), .sel(mem_wb_1_isjalwb));
  // Probe on WB

  // Other names for the same wires on the sheet: IMMI[5:0] = Func; IMMJ[15:0] = {IMMI, Func};
  //   JumpAddr[27:2] = {IMMJ, IMMI, Func}; Shamt[4:0] = IMMI[10:6]; RegD[4:0] = IMMI[15:11]; R2[4:0] = IMMJ[20:16];
  //   R1[4:0] = IMMJ[25:21]; PC_4[31:28] = JumpAddr; RSOut[1:0] = out_1; RTOut[1:0] = out_2

  // Notes on the sheet:
  //   contents of rom_1 (hex, n*v repeats v):
  //   34010001 211020 221820 2064000e 232822 aca4000e 8ca6000e c43824 10e10003 c7402a 11080001 201a0001
  //   20090001 8c0a000c ad4a0013 8c0a000c 1141fffb c000013 201b0001 23ff002c ac1f0000 308b0010 456027
  //   446825 97140 27842 8c100000 2000008 201c0001 800001d 201d0001 201e0001
endmodule

module ALU (
  input  [2:0] ALUCtl,
  input  [31:0] A,
  input  [31:0] B,
  input  [4:0] Shamt,
  output [31:0] ALUResult,
  output Zero,
  output Overflow
);

  wire comparator_1_lt, comparator_2_lt, comparator_3_eq, comparator_4_eq, or_2_out;
  wire [31:0] ADD, AND, NOR, OR, SLL, SLT, SLTU, SRL, SUB, XOR;

  assign XOR = A ^ B;  // XOR_Gate xor_1, 32 bits wide
  Adder #(.width(32)) adder_1 (.a(A), .b(B), .out(ADD));  // open: cin, cout
  Subtractor #(.width(32)) subtractor_1 (.a(A), .b(B), .out(SUB));  // open: bin, bout
  assign AND = A & B;  // AND_Gate and_1, 32 bits wide
  assign OR = A | B;  // OR_Gate or_1, 32 bits wide
  assign NOR = ~(A | B);  // NOR_Gate nor_1, 32 bits wide
  Comparator #(.width(32)) comparator_1 (.a(A), .b(B), .lt(comparator_1_lt));  // open: gt, eq
  assign SLT = {{31{1'b0}}, comparator_1_lt};  // Bit_Extender bit_extender_1
  Shifter #(.width(32)) shifter_1 (.in(B), .\dist (Shamt), .out(SLL));
  Shifter #(.width(32), .shift("lr")) shifter_2 (.in(B), .\dist (Shamt), .out(SRL));
  Comparator #(.width(32), .mode("unsigned")) comparator_2 (.a(A), .b(B), .lt(comparator_2_lt));  // open: gt, eq
  assign SLTU = {{31{1'b0}}, comparator_2_lt};  // Bit_Extender bit_extender_2
  Multiplexer #(.select(3), .width(32), .enable("false")) multiplexer_1 (
    .in0(NOR), .in1(AND), .in2(SUB), .in3(SLT), .in4(OR), .in5(ADD), .in6(SLL), .in7(SRL), .out(ALUResult),
    .sel(ALUCtl));
  Comparator #(.width(3)) comparator_3 (.a(3'b101), .b(ALUCtl), .eq(comparator_3_eq));  // open: gt, lt
  Comparator #(.width(3)) comparator_4 (.a(ALUCtl), .b(3'b010), .eq(comparator_4_eq));  // open: gt, lt
  Overflow_Unit overflow_unit_1 (
    .Add(comparator_3_eq), .Sub(comparator_4_eq), .ASign(A[31]), .BSign(B[31]), .ResultSign(ALUResult[31]),
    .Overflow(Overflow));
  or or_2 (or_2_out, ALUResult[0], ALUResult[1], ALUResult[2], ALUResult[3], ALUResult[4], ALUResult[5], ALUResult[6], ALUResult[7], ALUResult[8], ALUResult[9], ALUResult[10], ALUResult[11], ALUResult[12], ALUResult[13], ALUResult[14], ALUResult[15], ALUResult[16], ALUResult[17], ALUResult[18], ALUResult[19], ALUResult[20], ALUResult[21], ALUResult[22], ALUResult[23], ALUResult[24], ALUResult[25], ALUResult[26], ALUResult[27], ALUResult[28], ALUResult[29], ALUResult[30], ALUResult[31]);
  not not_1 (Zero, or_2_out);

  // Other names for the same wires on the sheet: ASign = A[31]; ResultSign = ALUResult[31]; BSign = B[31]

  // Notes on the sheet:
  //   ALUCtl for ADD on top port
  //   ALUCtl for SUB on second port
endmodule

module Register_File (
  input  [4:0] WrAddr,
  input  [31:0] WrData,
  input  WrReg,
  input  [4:0] RdAddr1,
  input  [4:0] RdAddr2,
  input  Clock,
  output [31:0] RdData1,
  output [31:0] RdData2
);

  wire and_1_out, and_2_out, comparator_1_eq, comparator_2_eq, comparator_3_eq, comparator_4_eq, not_1_out,
       not_2_out, WrReg0, WrReg1, WrReg2, WrReg3, WrReg4, WrReg5, WrReg6, WrReg7, WrReg8, WrReg9, WrReg10,
       WrReg11, WrReg12, WrReg13, WrReg14, WrReg15, WrReg16, WrReg17, WrReg18, WrReg19, WrReg20, WrReg21,
       WrReg22, WrReg23, WrReg24, WrReg25, WrReg26, WrReg27, WrReg28, WrReg29, WrReg30, WrReg31;
  wire [31:0] multiplexer_1_out, multiplexer_2_out, RegData1, RegData2, RegData3, RegData4, RegData5,
       RegData6, RegData7, RegData8, RegData9, RegData10, RegData11, RegData12, RegData13, RegData14,
       RegData15, RegData16, RegData17, RegData18, RegData19, RegData20, RegData21, RegData22, RegData23,
       RegData24, RegData25, RegData26, RegData27, RegData28, RegData29, RegData30, RegData31;

  Demultiplexer #(.select(5), .enable("false")) demultiplexer_1 (
    .out0(WrReg0), .out1(WrReg1), .out2(WrReg2), .out3(WrReg3), .out4(WrReg4), .out5(WrReg5), .out6(WrReg6),
    .out7(WrReg7), .out8(WrReg8), .out9(WrReg9), .out10(WrReg10), .out11(WrReg11), .out12(WrReg12),
    .out13(WrReg13), .out14(WrReg14), .out15(WrReg15), .out16(WrReg16), .out17(WrReg17), .out18(WrReg18),
    .out19(WrReg19), .out20(WrReg20), .out21(WrReg21), .out22(WrReg22), .out23(WrReg23), .out24(WrReg24),
    .out25(WrReg25), .out26(WrReg26), .out27(WrReg27), .out28(WrReg28), .out29(WrReg29), .out30(WrReg30),
    .out31(WrReg31), .in(WrReg), .sel(WrAddr));
  // Probe on RegData4
  Register #(.width(32)) Reg4 (.D(WrData), .en(WrReg4), .Q(RegData4), .clk(Clock));  // open: clr
  // Probe on RegData8
  Register #(.width(32)) Reg8 (.D(WrData), .en(WrReg8), .Q(RegData8), .clk(Clock));  // open: clr
  // Probe on RegData12
  Register #(.width(32)) Reg12 (.D(WrData), .en(WrReg12), .Q(RegData12), .clk(Clock));  // open: clr
  // Probe on RegData16
  Register #(.width(32)) Reg16 (.D(WrData), .en(WrReg16), .Q(RegData16), .clk(Clock));  // open: clr
  // Probe on RegData20
  Register #(.width(32)) Reg20 (.D(WrData), .en(WrReg20), .Q(RegData20), .clk(Clock));  // open: clr
  // Probe on RegData24
  Register #(.width(32)) Reg24 (.D(WrData), .en(WrReg24), .Q(RegData24), .clk(Clock));  // open: clr
  // Probe on RegData28
  Register #(.width(32)) Reg28 (.D(WrData), .en(WrReg28), .Q(RegData28), .clk(Clock));  // open: clr
  Register #(.width(32)) Reg1 (.D(WrData), .en(WrReg1), .Q(RegData1), .clk(Clock));  // open: clr
  Register #(.width(32)) Reg5 (.D(WrData), .en(WrReg5), .Q(RegData5), .clk(Clock));  // open: clr
  Register #(.width(32)) Reg9 (.D(WrData), .en(WrReg9), .Q(RegData9), .clk(Clock));  // open: clr
  Register #(.width(32)) Reg13 (.D(WrData), .en(WrReg13), .Q(RegData13), .clk(Clock));  // open: clr
  Register #(.width(32)) Reg17 (.D(WrData), .en(WrReg17), .Q(RegData17), .clk(Clock));  // open: clr
  Register #(.width(32)) Reg21 (.D(WrData), .en(WrReg21), .Q(RegData21), .clk(Clock));  // open: clr
  Register #(.width(32)) Reg25 (.D(WrData), .en(WrReg25), .Q(RegData25), .clk(Clock));  // open: clr
  Register #(.width(32)) Reg29 (.D(WrData), .en(WrReg29), .Q(RegData29), .clk(Clock));  // open: clr
  // Probe on RegData1
  // Probe on RegData5
  // Probe on RegData9
  // Probe on RegData13
  // Probe on RegData17
  // Probe on RegData21
  // Probe on RegData25
  // Probe on RegData29
  // Probe on RegData2
  Register #(.width(32)) Reg2 (.D(WrData), .en(WrReg2), .Q(RegData2), .clk(Clock));  // open: clr
  // Probe on RegData6
  Register #(.width(32)) Reg6 (.D(WrData), .en(WrReg6), .Q(RegData6), .clk(Clock));  // open: clr
  // Probe on RegData10
  Register #(.width(32)) Reg10 (.D(WrData), .en(WrReg10), .Q(RegData10), .clk(Clock));  // open: clr
  // Probe on RegData14
  Register #(.width(32)) Reg14 (.D(WrData), .en(WrReg14), .Q(RegData14), .clk(Clock));  // open: clr
  // Probe on RegData18
  Register #(.width(32)) Reg18 (.D(WrData), .en(WrReg18), .Q(RegData18), .clk(Clock));  // open: clr
  // Probe on RegData22
  Register #(.width(32)) Reg22 (.D(WrData), .en(WrReg22), .Q(RegData22), .clk(Clock));  // open: clr
  // Probe on RegData26
  Register #(.width(32)) Reg26 (.D(WrData), .en(WrReg26), .Q(RegData26), .clk(Clock));  // open: clr
  // Probe on RegData30
  Register #(.width(32)) Reg30 (.D(WrData), .en(WrReg30), .Q(RegData30), .clk(Clock));  // open: clr
  // Probe on RegData3
  Register #(.width(32)) Reg3 (.D(WrData), .en(WrReg3), .Q(RegData3), .clk(Clock));  // open: clr
  // Probe on RegData7
  Register #(.width(32)) Reg7 (.D(WrData), .en(WrReg7), .Q(RegData7), .clk(Clock));  // open: clr
  // Probe on RegData11
  Register #(.width(32)) Reg11 (.D(WrData), .en(WrReg11), .Q(RegData11), .clk(Clock));  // open: clr
  // Probe on RegData15
  Register #(.width(32)) Reg15 (.D(WrData), .en(WrReg15), .Q(RegData15), .clk(Clock));  // open: clr
  // Probe on RegData19
  Register #(.width(32)) Reg19 (.D(WrData), .en(WrReg19), .Q(RegData19), .clk(Clock));  // open: clr
  // Probe on RegData23
  Register #(.width(32)) Reg23 (.D(WrData), .en(WrReg23), .Q(RegData23), .clk(Clock));  // open: clr
  // Probe on RegData27
  Register #(.width(32)) Reg27 (.D(WrData), .en(WrReg27), .Q(RegData27), .clk(Clock));  // open: clr
  // Probe on RegData31
  Register #(.width(32)) Reg31 (.D(WrData), .en(WrReg31), .Q(RegData31), .clk(Clock));  // open: clr
  Multiplexer #(.select(5), .width(32), .enable("false")) multiplexer_1 (
    .in0({32{1'b0}}), .in1(RegData1), .in2(RegData2), .in3(RegData3), .in4(RegData4), .in5(RegData5),
    .in6(RegData6), .in7(RegData7), .in8(RegData8), .in9(RegData9), .in10(RegData10), .in11(RegData11),
    .in12(RegData12), .in13(RegData13), .in14(RegData14), .in15(RegData15), .in16(RegData16),
    .in17(RegData17), .in18(RegData18), .in19(RegData19), .in20(RegData20), .in21(RegData21),
    .in22(RegData22), .in23(RegData23), .in24(RegData24), .in25(RegData25), .in26(RegData26),
    .in27(RegData27), .in28(RegData28), .in29(RegData29), .in30(RegData30), .in31(RegData31),
    .out(multiplexer_1_out), .sel(RdAddr1));
  Multiplexer #(.select(5), .width(32), .enable("false")) multiplexer_2 (
    .in0({32{1'b0}}), .in1(RegData1), .in2(RegData2), .in3(RegData3), .in4(RegData4), .in5(RegData5),
    .in6(RegData6), .in7(RegData7), .in8(RegData8), .in9(RegData9), .in10(RegData10), .in11(RegData11),
    .in12(RegData12), .in13(RegData13), .in14(RegData14), .in15(RegData15), .in16(RegData16),
    .in17(RegData17), .in18(RegData18), .in19(RegData19), .in20(RegData20), .in21(RegData21),
    .in22(RegData22), .in23(RegData23), .in24(RegData24), .in25(RegData25), .in26(RegData26),
    .in27(RegData27), .in28(RegData28), .in29(RegData29), .in30(RegData30), .in31(RegData31),
    .out(multiplexer_2_out), .sel(RdAddr2));
  Multiplexer #(.width(32), .enable("false")) multiplexer_3 (
    .in0(multiplexer_1_out), .in1(WrData), .out(RdData1), .sel(and_1_out));
  Comparator #(.width(5), .mode("unsigned")) comparator_1 (
    .a(WrAddr), .b(RdAddr2), .eq(comparator_1_eq));  // open: gt, lt
  Multiplexer #(.width(32), .enable("false")) multiplexer_4 (
    .in0(multiplexer_2_out), .in1(WrData), .out(RdData2), .sel(and_2_out));
  Comparator #(.width(5), .mode("unsigned")) comparator_2 (
    .a(WrAddr), .b(RdAddr1), .eq(comparator_2_eq));  // open: gt, lt
  and and_1 (and_1_out, comparator_2_eq, WrReg, not_1_out);
  and and_2 (and_2_out, comparator_1_eq, WrReg, not_2_out);
  Comparator #(.width(5), .mode("unsigned")) comparator_3 (
    .a(WrAddr), .b({5{1'b0}}), .eq(comparator_3_eq));  // open: gt, lt
  not not_1 (not_1_out, comparator_3_eq);
  Comparator #(.width(5), .mode("unsigned")) comparator_4 (
    .a(WrAddr), .b({5{1'b0}}), .eq(comparator_4_eq));  // open: gt, lt
  not not_2 (not_2_out, comparator_4_eq);
endmodule

module Overflow_Unit (
  input  Add,
  input  Sub,
  input  ASign,
  input  BSign,
  input  ResultSign,
  output Overflow
);

  wire and_1_out, and_2_out, or_1_out, xnor_1_out, xor_1_out, xor_2_out;

  xnor xnor_1 (xnor_1_out, ASign, BSign);
  xor xor_1 (xor_1_out, ASign, BSign);
  and and_1 (and_1_out, xnor_1_out, Add);
  and and_2 (and_2_out, xor_1_out, Sub);
  or or_1 (or_1_out, and_1_out, and_2_out);
  xor xor_2 (xor_2_out, ResultSign, ASign);
  and and_3 (Overflow, or_1_out, xor_2_out);

  // Notes on the sheet:
  //   Overflow occurs when doing addition and sign(A) == sign(B) && sign(result) != sign(A)
  //   Or
  //   Overflow occurs when doing subtraction and sign(A) != sign(B) && sign(result) != sign(A)
endmodule

module IF_ID (
  input  [31:0] ADD,
  input  [31:0] ROM,
  input  CLK,
  input  clr,
  input  en,
  output [31:0] ADDout,
  output [31:0] OUT
);

  Register #(.width(32)) register_1 (.D(ADD), .en(en), .Q(ADDout), .clk(CLK), .clr(clr));
  Register #(.width(32)) register_2 (.D(ROM), .en(en), .Q(OUT), .clk(CLK), .clr(clr));
endmodule

module ID_EX (
  input  clk,
  input  clr,
  input  MemWriteID,
  input  [31:0] ImmID,
  input  [31:0] ShamtID,
  input  IsJALID,
  input  JumpID,
  input  [4:0] Shamt,
  input  [31:0] R1ID,
  input  [31:0] JumpAddr,
  input  BranchID,
  input  MemtoRegID,
  input  IsJRID,
  input  RegWriteID,
  input  [31:0] R2ID,
  input  [31:0] PCPlus4ID,
  input  BeqID,
  input  [2:0] ALUopID,
  input  ALUSrcID,
  input  [4:0] WriteReg_ID,
  input  MemReadID,
  input  En,
  output MemWriteEX,
  output [31:0] ImmEX,
  output [31:0] ShamtEX,
  output IsJALEX,
  output JumpEX,
  output [4:0] ShamtEX_2,
  output [31:0] R1EX,
  output [31:0] JumpAddr_2,
  output BranchEX,
  output MemtoRegEX,
  output IsJREX,
  output RegWriteEX,
  output [31:0] R2EX,
  output [31:0] PCPlusEX,
  output BneOrBeqEX,
  output [2:0] ALUopEX,
  output ALUSrcEX,
  output [4:0] WriteReg_EX,
  output MemReadEX
);

  Register #(.width(32)) register_1 (.D(ImmID), .en(En), .Q(ImmEX), .clk(clk), .clr(clr));
  Register #(.width(32)) register_2 (.D(R1ID), .en(En), .Q(R1EX), .clk(clk), .clr(clr));
  Register #(.width(32)) register_3 (.D(R2ID), .en(En), .Q(R2EX), .clk(clk), .clr(clr));
  Register #(.width(32)) register_4 (.D(ShamtID), .en(En), .Q(ShamtEX), .clk(clk), .clr(clr));
  Register #(.width(32)) register_5 (.D(JumpAddr), .en(En), .Q(JumpAddr_2), .clk(clk), .clr(clr));
  Register #(.width(32)) register_6 (.D(PCPlus4ID), .en(En), .Q(PCPlusEX), .clk(clk), .clr(clr));
  Register #(.width(1)) register_7 (.D(IsJALID), .en(En), .Q(IsJALEX), .clk(clk), .clr(clr));
  Register #(.width(5)) register_8 (.D(Shamt), .en(En), .Q(ShamtEX_2), .clk(clk), .clr(clr));
  Register #(.width(1)) register_9 (.D(MemtoRegID), .en(En), .Q(MemtoRegEX), .clk(clk), .clr(clr));
  Register #(.width(1)) register_10 (.D(RegWriteID), .en(En), .Q(RegWriteEX), .clk(clk), .clr(clr));
  Register #(.width(1)) register_11 (.D(BeqID), .en(En), .Q(BneOrBeqEX), .clk(clk), .clr(clr));
  Register #(.width(1)) register_12 (.D(ALUSrcID), .en(En), .Q(ALUSrcEX), .clk(clk), .clr(clr));
  Register #(.width(1)) register_13 (.D(MemReadID), .en(En), .Q(MemReadEX), .clk(clk), .clr(clr));
  Register #(.width(1)) register_14 (.D(MemWriteID), .en(En), .Q(MemWriteEX), .clk(clk), .clr(clr));
  Register #(.width(1)) register_15 (.D(JumpID), .en(En), .Q(JumpEX), .clk(clk), .clr(clr));
  Register #(.width(1)) register_16 (.D(BranchID), .en(En), .Q(BranchEX), .clk(clk), .clr(clr));
  Register #(.width(1)) register_17 (.D(IsJRID), .en(En), .Q(IsJREX), .clk(clk), .clr(clr));
  Register #(.width(3)) register_18 (.D(ALUopID), .en(En), .Q(ALUopEX), .clk(clk), .clr(clr));
  Register #(.width(5)) register_19 (.D(WriteReg_ID), .en(En), .Q(WriteReg_EX), .clk(clk), .clr(clr));
endmodule

// Control Unit
module Control (
  input  [5:0] op,
  input  [5:0] Funct,
  output IsJAL,
  output MemRead,
  output MemtoReg,
  output MemWrite,
  output [2:0] ALUop,
  output RegWrite,
  output Jump,
  output BneOrBeq,
  output Branch,
  output ALUSrc,
  output RegDst,
  output IsUnsigned,
  output JR,
  output ReadRs,
  output ReadRt
);

  wire fdecoder_1_jr, IsSpecial, not_1_out;
  wire [2:0] aludecoder_1_out0, fdecoder_1_out0;

  OpDecoder opdecoder_1 (
    .op0(op[5]), .op1(op[4]), .op2(op[3]), .op3(op[2]), .op4(op[1]), .op5(op[0]), .MemRead(MemRead),
    .MemWrite(MemWrite), .ALUSrc(ALUSrc), .Jump(Jump), .MemtoReg(MemtoReg), .Branch(Branch), .RegDst(RegDst),
    .RegWrite(RegWrite), .BneBeq(BneOrBeq), .IsJAL(IsJAL), .IsUnsigned(IsUnsigned));
  RegisterRead registerread_1 (
    .op0(op[5]), .op1(op[4]), .op2(op[3]), .op3(op[2]), .op4(op[1]), .op5(op[0]), .Funct0(Funct[5]),
    .Funct1(Funct[4]), .Funct2(Funct[3]), .Funct3(Funct[2]), .Funct4(Funct[1]), .Funct5(Funct[0]),
    .ReadRs(ReadRs), .ReadRt(ReadRt));
  ALUdecoder aludecoder_1 (
    .Op5(op[5]), .Op4(op[4]), .Op3(op[3]), .Op2(op[2]), .Op1(op[1]), .Op0(op[0]),
    .Out2(aludecoder_1_out0[2]), .Out1(aludecoder_1_out0[1]), .Out0(aludecoder_1_out0[0]));
  FDecoder fdecoder_1 (
    .F5(Funct[5]), .Out2(fdecoder_1_out0[2]), .F4(Funct[4]), .F3(Funct[3]), .F2(Funct[2]),
    .Out1(fdecoder_1_out0[1]), .F1(Funct[1]), .Out0(fdecoder_1_out0[0]), .F0(Funct[0]), .JR(fdecoder_1_jr));
  Multiplexer #(.enable("false")) multiplexer_1 (.in0(1'b0), .in1(fdecoder_1_jr), .out(JR), .sel(IsSpecial));
  not not_1 (not_1_out, IsSpecial);
  Multiplexer #(.width(3), .enable("false")) multiplexer_2 (
    .in0(fdecoder_1_out0), .in1(aludecoder_1_out0), .out(ALUop), .sel(not_1_out));
  and and_1 (IsSpecial, ~op[5], ~op[4], ~op[3], ~op[2], ~op[1], ~op[0]);  // AND_Gate

  // Other names for the same wires on the sheet: IsJR = JR
endmodule

module OpDecoder (
  input  op0,
  input  op1,
  input  op2,
  input  op3,
  input  op4,
  input  op5,
  output MemRead,
  output MemWrite,
  output ALUSrc,
  output Jump,
  output MemtoReg,
  output Branch,
  output RegDst,
  output RegWrite,
  output BneBeq,
  output IsJAL,
  output IsUnsigned
);

  wire and_3_out, and_4_out, and_5_out, and_6_out, and_7_out, and_8_out, and_9_out, and_10_out, and_11_out,
       and_12_out, and_14_out, and_15_out, and_17_out, and_18_out, and_19_out, and_20_out, and_21_out,
       and_22_out, and_23_out, and_24_out, and_25_out, and_26_out, not_1_out, not_2_out, not_3_out,
       not_4_out, not_5_out, not_6_out, not_7_out, not_8_out, not_9_out, not_10_out, not_11_out, not_12_out,
       not_13_out, not_14_out, not_15_out, not_16_out, not_17_out, not_18_out, not_19_out, not_20_out,
       not_21_out, not_22_out, not_23_out, not_24_out, not_25_out, not_26_out, not_27_out, not_28_out,
       not_29_out, not_30_out, not_31_out, not_32_out, not_33_out, not_34_out, not_35_out, not_36_out,
       not_37_out, not_38_out, not_39_out, not_40_out, not_41_out, not_42_out, not_43_out, not_44_out,
       not_45_out, not_46_out, not_47_out, not_48_out, not_49_out, not_50_out, not_51_out, not_52_out,
       not_53_out, not_54_out, not_55_out, not_56_out, not_57_out, not_58_out, not_59_out, not_60_out,
       not_61_out, not_62_out, not_63_out, not_64_out, not_65_out, not_66_out, not_67_out, not_68_out,
       not_69_out, not_70_out, not_71_out, not_72_out, not_73_out, not_74_out, not_75_out, not_76_out,
       not_77_out, not_78_out, not_79_out, not_80_out, not_81_out, not_82_out, not_83_out, not_84_out,
       not_85_out, not_86_out, not_87_out, not_88_out, not_89_out, not_90_out, not_91_out, not_92_out,
       not_93_out, not_94_out, not_95_out, not_96_out, not_97_out, not_98_out, not_99_out, not_100_out,
       not_101_out, not_102_out, not_103_out, not_104_out, not_105_out, not_106_out, not_107_out,
       not_108_out, not_109_out, not_110_out, not_111_out, not_112_out, not_113_out, not_114_out,
       not_115_out, not_116_out, not_117_out;

  not not_1 (not_1_out, op1);
  not not_2 (not_2_out, op2);
  not not_3 (not_3_out, op3);
  not not_4 (not_4_out, op1);
  not not_5 (not_5_out, op3);
  not not_6 (not_6_out, op0);
  not not_7 (not_7_out, op1);
  not not_8 (not_8_out, op3);
  not not_9 (not_9_out, op4);
  not not_10 (not_10_out, op5);
  not not_11 (not_11_out, op1);
  not not_12 (not_12_out, op2);
  not not_13 (not_13_out, op3);
  not not_14 (not_14_out, op1);
  not not_15 (not_15_out, op3);
  not not_16 (not_16_out, op0);
  not not_17 (not_17_out, op1);
  not not_18 (not_18_out, op4);
  not not_19 (not_19_out, op5);
  not not_20 (not_20_out, op0);
  not not_21 (not_21_out, op1);
  not not_22 (not_22_out, op4);
  not not_23 (not_23_out, op0);
  not not_24 (not_24_out, op1);
  not not_25 (not_25_out, op3);
  not not_26 (not_26_out, op5);
  not not_27 (not_27_out, op0);
  not not_28 (not_28_out, op1);
  not not_29 (not_29_out, op3);
  not not_30 (not_30_out, op4);
  not not_31 (not_31_out, op0);
  not not_32 (not_32_out, op1);
  not not_33 (not_33_out, op3);
  not not_34 (not_34_out, op4);
  not not_35 (not_35_out, op5);
  not not_36 (not_36_out, op0);
  not not_37 (not_37_out, op1);
  not not_38 (not_38_out, op2);
  not not_39 (not_39_out, op3);
  not not_40 (not_40_out, op5);
  not not_41 (not_41_out, op0);
  not not_42 (not_42_out, op1);
  not not_43 (not_43_out, op2);
  not not_44 (not_44_out, op3);
  not not_45 (not_45_out, op1);
  not not_46 (not_46_out, op2);
  not not_47 (not_47_out, op3);
  not not_48 (not_48_out, op0);
  not not_49 (not_49_out, op1);
  not not_50 (not_50_out, op2);
  not not_51 (not_51_out, op4);
  not not_52 (not_52_out, op0);
  not not_53 (not_53_out, op1);
  not not_54 (not_54_out, op2);
  not not_55 (not_55_out, op4);
  not not_56 (not_56_out, op5);
  not not_57 (not_57_out, op0);
  not not_58 (not_58_out, op1);
  not not_59 (not_59_out, op2);
  not not_60 (not_60_out, op3);
  not not_61 (not_61_out, op4);
  not not_62 (not_62_out, op5);
  not not_63 (not_63_out, op0);
  not not_64 (not_64_out, op1);
  not not_65 (not_65_out, op2);
  not not_66 (not_66_out, op3);
  not not_67 (not_67_out, op4);
  not not_68 (not_68_out, op5);
  not not_69 (not_69_out, op0);
  not not_70 (not_70_out, op1);
  not not_71 (not_71_out, op3);
  not not_72 (not_72_out, op4);
  not not_73 (not_73_out, op5);
  not not_74 (not_74_out, op1);
  not not_75 (not_75_out, op2);
  not not_76 (not_76_out, op3);
  not not_77 (not_77_out, op0);
  not not_78 (not_78_out, op1);
  not not_79 (not_79_out, op4);
  not not_80 (not_80_out, op5);
  not not_81 (not_81_out, op0);
  not not_82 (not_82_out, op1);
  not not_83 (not_83_out, op4);
  not not_84 (not_84_out, op0);
  not not_85 (not_85_out, op1);
  not not_86 (not_86_out, op3);
  not not_87 (not_87_out, op5);
  not not_88 (not_88_out, op0);
  not not_89 (not_89_out, op1);
  not not_90 (not_90_out, op3);
  not not_91 (not_91_out, op4);
  not not_92 (not_92_out, op0);
  not not_93 (not_93_out, op1);
  not not_94 (not_94_out, op3);
  not not_95 (not_95_out, op4);
  not not_96 (not_96_out, op5);
  not not_97 (not_97_out, op0);
  not not_98 (not_98_out, op1);
  not not_99 (not_99_out, op2);
  not not_100 (not_100_out, op3);
  not not_101 (not_101_out, op0);
  not not_102 (not_102_out, op2);
  not not_103 (not_103_out, op3);
  not not_104 (not_104_out, op4);
  not not_105 (not_105_out, op5);
  not not_106 (not_106_out, op0);
  not not_107 (not_107_out, op1);
  not not_108 (not_108_out, op2);
  not not_109 (not_109_out, op4);
  not not_110 (not_110_out, op0);
  not not_111 (not_111_out, op1);
  not not_112 (not_112_out, op2);
  not not_113 (not_113_out, op3);
  not not_114 (not_114_out, op0);
  not not_115 (not_115_out, op1);
  not not_116 (not_116_out, op3);
  not not_117 (not_117_out, op4);
  and and_1 (MemRead, op0, not_1_out, not_2_out, not_3_out, op4, op5);
  and and_2 (MemWrite, op0, not_4_out, op2, not_5_out, op4, op5);
  and and_3 (and_3_out, not_6_out, not_7_out, op2, not_8_out, not_9_out, not_10_out);
  and and_4 (and_4_out, op0, not_11_out, not_12_out, not_13_out, op4, op5);
  and and_5 (and_5_out, op0, not_14_out, op2, not_15_out, op4, op5);
  and and_6 (and_6_out, not_16_out, not_17_out, op2, op3, not_18_out, not_19_out);
  and and_7 (and_7_out, not_20_out, not_21_out, op2, op3, not_22_out, op5);
  and and_8 (and_8_out, not_23_out, not_24_out, op2, not_25_out, op4, not_26_out);
  and and_9 (and_9_out, not_27_out, not_28_out, op2, not_29_out, not_30_out, op5);
  and and_10 (and_10_out, not_31_out, not_32_out, op2, not_33_out, not_34_out, not_35_out);
  and and_11 (and_11_out, not_36_out, not_37_out, not_38_out, not_39_out, op4, not_40_out);
  and and_12 (and_12_out, not_41_out, not_42_out, not_43_out, not_44_out, op4, op5);
  and and_13 (MemtoReg, op0, not_45_out, not_46_out, not_47_out, op4, op5);
  and and_14 (and_14_out, not_48_out, not_49_out, not_50_out, op3, not_51_out, op5);
  and and_15 (and_15_out, not_52_out, not_53_out, not_54_out, op3, not_55_out, not_56_out);
  and and_16 (RegDst, not_57_out, not_58_out, not_59_out, not_60_out, not_61_out, not_62_out);
  and and_17 (and_17_out, not_63_out, not_64_out, not_65_out, not_66_out, not_67_out, not_68_out);
  and and_18 (and_18_out, not_69_out, not_70_out, op2, not_71_out, not_72_out, not_73_out);
  and and_19 (and_19_out, op0, not_74_out, not_75_out, not_76_out, op4, op5);
  and and_20 (and_20_out, not_77_out, not_78_out, op2, op3, not_79_out, not_80_out);
  and and_21 (and_21_out, not_81_out, not_82_out, op2, op3, not_83_out, op5);
  and and_22 (and_22_out, not_84_out, not_85_out, op2, not_86_out, op4, not_87_out);
  and and_23 (and_23_out, not_88_out, not_89_out, op2, not_90_out, not_91_out, op5);
  and and_24 (and_24_out, not_92_out, not_93_out, op2, not_94_out, not_95_out, not_96_out);
  and and_25 (and_25_out, not_97_out, not_98_out, not_99_out, not_100_out, op4, op5);
  and and_26 (and_26_out, not_101_out, op1, not_102_out, not_103_out, not_104_out, not_105_out);
  and and_27 (BneBeq, not_106_out, not_107_out, not_108_out, op3, not_109_out, op5);
  and and_28 (IsJAL, not_110_out, not_111_out, not_112_out, not_113_out, op4, op5);
  and and_29 (IsUnsigned, not_114_out, not_115_out, op2, not_116_out, not_117_out, op5);
  or or_1 (ALUSrc, and_3_out, and_4_out, and_5_out, and_6_out, and_7_out, and_8_out, and_9_out, and_10_out);
  or or_2 (Jump, and_11_out, and_12_out);
  or or_3 (Branch, and_14_out, and_15_out);
  or or_4 (RegWrite, and_17_out, and_18_out, and_19_out, and_20_out, and_21_out, and_22_out, and_23_out, and_24_out, and_25_out, and_26_out);
endmodule

module ALUDecoder (
  input  Op5,
  input  Op4,
  input  Op3,
  input  Op2,
  input  Op1,
  input  Op0,
  input  Func5,
  input  Func4,
  input  Func3,
  input  Func2,
  input  Func1,
  input  Func0,
  output Out2,
  output Out1,
  output Out0
);

  wire and_1_out, and_2_out, and_3_out, and_4_out, and_5_out, and_6_out, and_7_out, and_8_out, not_1_out,
       not_2_out, not_3_out, not_4_out, not_5_out, not_6_out, not_7_out, not_8_out, not_9_out, not_10_out,
       not_11_out, not_12_out, not_13_out, not_14_out, not_15_out;

  not not_1 (not_1_out, Op2);
  not not_2 (not_2_out, Func2);
  not not_3 (not_3_out, Func1);
  not not_4 (not_4_out, Op2);
  not not_5 (not_5_out, Func1);
  not not_6 (not_6_out, Op2);
  not not_7 (not_7_out, Op5);
  not not_8 (not_8_out, Op3);
  not not_9 (not_9_out, Func2);
  not not_10 (not_10_out, Op3);
  not not_11 (not_11_out, Op2);
  not not_12 (not_12_out, Func1);
  not not_13 (not_13_out, Func0);
  not not_14 (not_14_out, Op2);
  not not_15 (not_15_out, Op0);
  and and_1 (and_1_out, not_1_out, not_2_out, not_3_out);
  and and_2 (and_2_out, not_4_out, not_5_out, Func0);
  and and_3 (and_3_out, Op3, not_6_out);
  and and_4 (and_4_out, not_7_out, not_8_out, not_9_out, Func1);
  and and_5 (and_5_out, not_10_out, Op2);
  and and_6 (and_6_out, not_11_out, not_12_out, not_13_out);
  and and_7 (and_7_out, not_14_out, Func3);
  and and_8 (and_8_out, Op3, not_15_out);
  or or_1 (Out2, and_1_out, and_2_out, Op0, and_3_out);
  or or_2 (Out1, and_4_out, and_5_out);
  or or_3 (Out0, and_6_out, and_7_out, and_8_out, Op5);
endmodule

// ALUDecoder
module ALUdecoder (
  input  Op5,
  input  Op4,
  input  Op3,
  input  Op2,
  input  Op1,
  input  Op0,
  output Out2,
  output Out1,
  output Out0
);

  wire and_2_out, not_1_out, not_2_out, not_3_out, not_4_out, not_5_out;

  not not_1 (not_1_out, Op2);
  not not_2 (not_2_out, Op3);
  not not_3 (not_3_out, Op1);
  not not_4 (not_4_out, Op0);
  or or_1 (Out2, not_1_out, Op0);
  and and_1 (Out1, not_2_out, not_3_out);
  not not_5 (not_5_out, Op2);
  and and_2 (and_2_out, Op3, not_4_out);
  or or_2 (Out0, not_5_out, and_2_out);
endmodule

// Func Decoder
module FuncDecoder (
  input  Func5,
  input  Func4,
  input  Func3,
  input  Func2,
  input  Func1,
  input  Func0,
  output Out2,
  output Out1,
  output Out0,
  output JR
);

  wire and_1_out, and_2_out, and_4_out, not_1_out, not_2_out, not_3_out, not_4_out, not_5_out, not_6_out,
       not_7_out, not_8_out, not_9_out, not_10_out;

  not not_1 (not_1_out, Func2);
  not not_2 (not_2_out, Func1);
  not not_3 (not_3_out, Func1);
  not not_4 (not_4_out, Func2);
  not not_5 (not_5_out, Func1);
  not not_6 (not_6_out, Func0);
  not not_7 (not_7_out, Func5);
  not not_8 (not_8_out, Func4);
  not not_9 (not_9_out, Func2);
  not not_10 (not_10_out, Func1);
  and and_1 (and_1_out, not_1_out, not_2_out);
  and and_2 (and_2_out, not_3_out, Func0);
  and and_3 (Out1, not_4_out, Func1);
  and and_4 (and_4_out, not_5_out, not_6_out);
  and and_5 (JR, not_7_out, not_8_out, Func3, not_9_out, not_10_out, Func0);
  or or_1 (Out2, and_1_out, and_2_out);
  or or_2 (Out0, and_4_out, Func3);
endmodule

module RegisterRead (
  input  op0,
  input  op1,
  input  op2,
  input  op3,
  input  op4,
  input  op5,
  input  Funct0,
  input  Funct1,
  input  Funct2,
  input  Funct3,
  input  Funct4,
  input  Funct5,
  output ReadRs,
  output ReadRt
);

  wire and_1_out, and_2_out, and_3_out, and_4_out, and_5_out, and_6_out, and_7_out, and_8_out, and_9_out,
       and_10_out, and_11_out, and_12_out, and_13_out, and_14_out, and_15_out, and_16_out, and_17_out,
       and_18_out, and_19_out, and_20_out, and_21_out, and_22_out, and_23_out, and_24_out, and_25_out,
       and_26_out, and_27_out, and_28_out, and_29_out, and_30_out, and_31_out, and_32_out, and_33_out,
       and_34_out, and_35_out, not_1_out, not_2_out, not_3_out, not_4_out, not_5_out, not_6_out, not_7_out,
       not_8_out, not_9_out, not_10_out, not_11_out, not_12_out, not_13_out, not_14_out, not_15_out,
       not_16_out, not_17_out, not_18_out, not_19_out, not_20_out, not_21_out, not_22_out, not_23_out,
       not_24_out, not_25_out, not_26_out, not_27_out, not_28_out, not_29_out, not_30_out, not_31_out,
       not_32_out, not_33_out, not_34_out, not_35_out, not_36_out, not_37_out, not_38_out, not_39_out,
       not_40_out, not_41_out, not_42_out, not_43_out, not_44_out, not_45_out, not_46_out, not_47_out,
       not_48_out, not_49_out, not_50_out, not_51_out, not_52_out, not_53_out, not_54_out, not_55_out,
       not_56_out, not_57_out, not_58_out, not_59_out, not_60_out, not_61_out, not_62_out, not_63_out,
       not_64_out, not_65_out, not_66_out, not_67_out, not_68_out, not_69_out, not_70_out, not_71_out,
       not_72_out, not_73_out, not_74_out, not_75_out, not_76_out, not_77_out, not_78_out, not_79_out,
       not_80_out, not_81_out, not_82_out, not_83_out, not_84_out, not_85_out, not_86_out, not_87_out,
       not_88_out, not_89_out, not_90_out, not_91_out, not_92_out, not_93_out, not_94_out, not_95_out,
       not_96_out, not_97_out, not_98_out, not_99_out, not_100_out, not_101_out, not_102_out, not_103_out,
       not_104_out, not_105_out, not_106_out, not_107_out, not_108_out, not_109_out, not_110_out,
       not_111_out, not_112_out, not_113_out, not_114_out, not_115_out, not_116_out, not_117_out,
       not_118_out, not_119_out, not_120_out, not_121_out, not_122_out, not_123_out, not_124_out,
       not_125_out, not_126_out, not_127_out, not_128_out, not_129_out, not_130_out, not_131_out,
       not_132_out, not_133_out, not_134_out, not_135_out, not_136_out, or_1_out, or_2_out;

  not not_1 (not_1_out, Funct1);
  not not_2 (not_2_out, Funct2);
  not not_3 (not_3_out, Funct3);
  not not_4 (not_4_out, Funct4);
  not not_5 (not_5_out, Funct5);
  not not_6 (not_6_out, Funct1);
  not not_7 (not_7_out, Funct2);
  not not_8 (not_8_out, Funct4);
  not not_9 (not_9_out, Funct5);
  not not_10 (not_10_out, Funct1);
  not not_11 (not_11_out, Funct2);
  not not_12 (not_12_out, Funct3);
  not not_13 (not_13_out, Funct4);
  not not_14 (not_14_out, Funct1);
  not not_15 (not_15_out, Funct2);
  not not_16 (not_16_out, Funct3);
  not not_17 (not_17_out, Funct5);
  not not_18 (not_18_out, Funct1);
  not not_19 (not_19_out, Funct2);
  not not_20 (not_20_out, Funct4);
  not not_21 (not_21_out, Funct1);
  not not_22 (not_22_out, Funct2);
  not not_23 (not_23_out, Funct1);
  not not_24 (not_24_out, Funct3);
  not not_25 (not_25_out, Funct5);
  not not_26 (not_26_out, Funct1);
  not not_27 (not_27_out, Funct3);
  not not_28 (not_28_out, Funct0);
  not not_29 (not_29_out, Funct1);
  not not_30 (not_30_out, Funct3);
  not not_31 (not_31_out, Funct4);
  not not_32 (not_32_out, Funct5);
  not not_33 (not_33_out, Funct1);
  not not_34 (not_34_out, Funct2);
  not not_35 (not_35_out, Funct3);
  not not_36 (not_36_out, Funct4);
  not not_37 (not_37_out, Funct5);
  not not_38 (not_38_out, Funct1);
  not not_39 (not_39_out, Funct2);
  not not_40 (not_40_out, Funct3);
  not not_41 (not_41_out, Funct4);
  not not_42 (not_42_out, Funct1);
  not not_43 (not_43_out, Funct2);
  not not_44 (not_44_out, Funct4);
  not not_45 (not_45_out, Funct5);
  not not_46 (not_46_out, Funct0);
  not not_47 (not_47_out, Funct1);
  not not_48 (not_48_out, Funct2);
  not not_49 (not_49_out, Funct3);
  not not_50 (not_50_out, Funct4);
  not not_51 (not_51_out, Funct5);
  not not_52 (not_52_out, Funct0);
  not not_53 (not_53_out, Funct1);
  not not_54 (not_54_out, Funct2);
  not not_55 (not_55_out, Funct3);
  not not_56 (not_56_out, Funct0);
  not not_57 (not_57_out, Funct1);
  not not_58 (not_58_out, Funct2);
  not not_59 (not_59_out, Funct3);
  not not_60 (not_60_out, Funct5);
  not not_61 (not_61_out, Funct1);
  not not_62 (not_62_out, Funct2);
  not not_63 (not_63_out, Funct3);
  not not_64 (not_64_out, Funct5);
  not not_65 (not_65_out, Funct1);
  not not_66 (not_66_out, Funct2);
  not not_67 (not_67_out, Funct4);
  not not_68 (not_68_out, Funct1);
  not not_69 (not_69_out, Funct2);
  not not_70 (not_70_out, Funct1);
  not not_71 (not_71_out, Funct3);
  not not_72 (not_72_out, Funct5);
  not not_73 (not_73_out, Funct1);
  not not_74 (not_74_out, Funct3);
  and and_1 (and_1_out, Funct0, not_1_out, not_2_out, not_3_out, not_4_out, not_5_out);
  and and_2 (and_2_out, Funct0, not_6_out, not_7_out, Funct3, not_8_out, not_9_out);
  and and_3 (and_3_out, Funct0, not_10_out, not_11_out, not_12_out, not_13_out, Funct5);
  and and_4 (and_4_out, Funct0, not_14_out, not_15_out, not_16_out, Funct4, not_17_out);
  and and_5 (and_5_out, Funct0, not_18_out, not_19_out, Funct3, not_20_out, Funct5);
  and and_6 (and_6_out, Funct0, not_21_out, not_22_out, Funct3, Funct4, Funct5);
  and and_7 (and_7_out, Funct0, not_23_out, Funct2, not_24_out, Funct4, not_25_out);
  and and_8 (and_8_out, Funct0, not_26_out, Funct2, not_27_out, Funct4, Funct5);
  and and_9 (and_9_out, not_28_out, not_29_out, Funct2, not_30_out, not_31_out, not_32_out);
  and and_10 (and_10_out, Funct0, not_33_out, not_34_out, not_35_out, not_36_out, not_37_out);
  and and_11 (and_11_out, Funct0, not_38_out, not_39_out, not_40_out, not_41_out, Funct5);
  and and_12 (and_12_out, Funct0, not_42_out, not_43_out, Funct3, not_44_out, not_45_out);
  and and_13 (and_13_out, not_46_out, not_47_out, not_48_out, not_49_out, not_50_out, not_51_out);
  and and_14 (and_14_out, not_52_out, not_53_out, not_54_out, not_55_out, Funct4, Funct5);
  and and_15 (and_15_out, not_56_out, not_57_out, not_58_out, not_59_out, Funct4, not_60_out);
  and and_16 (and_16_out, Funct0, not_61_out, not_62_out, not_63_out, Funct4, not_64_out);
  and and_17 (and_17_out, Funct0, not_65_out, not_66_out, Funct3, not_67_out, Funct5);
  and and_18 (and_18_out, Funct0, not_68_out, not_69_out, Funct3, Funct4, Funct5);
  and and_19 (and_19_out, Funct0, not_70_out, Funct2, not_71_out, Funct4, not_72_out);
  and and_20 (and_20_out, Funct0, not_73_out, Funct2, not_74_out, Funct4, Funct5);
  not not_75 (not_75_out, op0);
  not not_76 (not_76_out, op1);
  not not_77 (not_77_out, op2);
  not not_78 (not_78_out, op3);
  not not_79 (not_79_out, op4);
  not not_80 (not_80_out, op5);
  or or_1 (or_1_out, and_1_out, and_2_out, and_3_out, and_4_out, and_5_out, and_6_out, and_7_out, and_8_out, and_9_out);
  not not_81 (not_81_out, op0);
  not not_82 (not_82_out, op1);
  not not_83 (not_83_out, op3);
  not not_84 (not_84_out, op4);
  not not_85 (not_85_out, op5);
  not not_86 (not_86_out, op0);
  not not_87 (not_87_out, op1);
  not not_88 (not_88_out, op3);
  not not_89 (not_89_out, op4);
  not not_90 (not_90_out, op0);
  not not_91 (not_91_out, op1);
  not not_92 (not_92_out, op4);
  not not_93 (not_93_out, op5);
  not not_94 (not_94_out, op0);
  not not_95 (not_95_out, op1);
  not not_96 (not_96_out, op4);
  not not_97 (not_97_out, op1);
  not not_98 (not_98_out, op2);
  not not_99 (not_99_out, op3);
  not not_100 (not_100_out, op0);
  not not_101 (not_101_out, op1);
  not not_102 (not_102_out, op2);
  not not_103 (not_103_out, op4);
  not not_104 (not_104_out, op5);
  not not_105 (not_105_out, op0);
  not not_106 (not_106_out, op1);
  not not_107 (not_107_out, op2);
  not not_108 (not_108_out, op4);
  not not_109 (not_109_out, op0);
  not not_110 (not_110_out, op1);
  not not_111 (not_111_out, op3);
  not not_112 (not_112_out, op5);
  not not_113 (not_113_out, op1);
  not not_114 (not_114_out, op3);
  not not_115 (not_115_out, op0);
  not not_116 (not_116_out, op1);
  not not_117 (not_117_out, op2);
  not not_118 (not_118_out, op3);
  not not_119 (not_119_out, op4);
  not not_120 (not_120_out, op5);
  or or_2 (or_2_out, and_10_out, and_11_out, and_12_out, and_13_out, and_14_out, and_15_out, and_16_out, and_17_out, and_18_out, and_19_out, and_20_out);
  not not_121 (not_121_out, op0);
  not not_122 (not_122_out, op1);
  not not_123 (not_123_out, op2);
  not not_124 (not_124_out, op4);
  not not_125 (not_125_out, op5);
  not not_126 (not_126_out, op0);
  not not_127 (not_127_out, op1);
  not not_128 (not_128_out, op2);
  not not_129 (not_129_out, op4);
  not not_130 (not_130_out, op0);
  not not_131 (not_131_out, op2);
  not not_132 (not_132_out, op3);
  not not_133 (not_133_out, op4);
  not not_134 (not_134_out, op5);
  not not_135 (not_135_out, op1);
  not not_136 (not_136_out, op3);
  and and_21 (and_21_out, not_75_out, not_76_out, not_77_out, not_78_out, not_79_out, not_80_out, or_1_out);
  and and_22 (and_22_out, not_81_out, not_82_out, op2, not_83_out, not_84_out, not_85_out);
  and and_23 (and_23_out, not_86_out, not_87_out, op2, not_88_out, not_89_out, op5);
  and and_24 (and_24_out, not_90_out, not_91_out, op2, op3, not_92_out, not_93_out);
  and and_25 (and_25_out, not_94_out, not_95_out, op2, op3, not_96_out, op5);
  and and_26 (and_26_out, op0, not_97_out, not_98_out, not_99_out, op4, op5);
  and and_27 (and_27_out, not_100_out, not_101_out, not_102_out, op3, not_103_out, not_104_out);
  and and_28 (and_28_out, not_105_out, not_106_out, not_107_out, op3, not_108_out, op5);
  and and_29 (and_29_out, not_109_out, not_110_out, op2, not_111_out, op4, not_112_out);
  and and_30 (and_30_out, op0, not_113_out, op2, not_114_out, op4, op5);
  and and_31 (and_31_out, not_115_out, not_116_out, not_117_out, not_118_out, not_119_out, not_120_out, or_2_out);
  and and_32 (and_32_out, not_121_out, not_122_out, not_123_out, op3, not_124_out, not_125_out);
  and and_33 (and_33_out, not_126_out, not_127_out, not_128_out, op3, not_129_out, op5);
  and and_34 (and_34_out, not_130_out, op1, not_131_out, not_132_out, not_133_out, not_134_out);
  and and_35 (and_35_out, op0, not_135_out, op2, not_136_out, op4, op5);
  or or_3 (ReadRs, and_21_out, and_22_out, and_23_out, and_24_out, and_25_out, and_26_out, and_27_out, and_28_out, and_29_out, and_30_out);
  or or_4 (ReadRt, and_31_out, and_32_out, and_33_out, and_34_out, and_35_out);
endmodule

module EX_MEM (
  input  clk,
  input  clr,
  input  IsJALEX,
  input  [31:0] ALUResultEX,
  input  MemtoRegEX,
  input  RegWriteEX,
  input  [31:0] WriteDataEX,
  input  ZeroEX,
  input  [31:0] JumpAddrEX,
  input  MemReadEX,
  input  MemWriteEX,
  input  [4:0] WriteReg_EX,
  input  En,
  output IsJALMEM,
  output [31:0] ALUResultMEM,
  output MemtoRegMEM,
  output RegWriteMEM,
  output [31:0] WriteDataMEM,
  output ZeroMEM,
  output [31:0] JumpAddrMEM,
  output MemReadMEM,
  output MemWriteMEM,
  output [4:0] WriteReg_MEM
);

  Register #(.width(1)) register_1 (.D(IsJALEX), .en(En), .Q(IsJALMEM), .clk(clk), .clr(clr));
  Register #(.width(1)) register_2 (.D(MemtoRegEX), .en(En), .Q(MemtoRegMEM), .clk(clk), .clr(clr));
  Register #(.width(1)) register_3 (.D(RegWriteEX), .en(En), .Q(RegWriteMEM), .clk(clk), .clr(clr));
  Register #(.width(1)) register_4 (.D(ZeroEX), .en(En), .Q(ZeroMEM), .clk(clk), .clr(clr));
  Register #(.width(1)) register_5 (.D(MemReadEX), .en(En), .Q(MemReadMEM), .clk(clk), .clr(clr));
  Register #(.width(1)) register_6 (.D(MemWriteEX), .en(En), .Q(MemWriteMEM), .clk(clk), .clr(clr));
  Register #(.width(5)) register_7 (.D(WriteReg_EX), .en(En), .Q(WriteReg_MEM), .clk(clk), .clr(clr));
  Register #(.width(32)) register_8 (.D(ALUResultEX), .en(En), .Q(ALUResultMEM), .clk(clk), .clr(clr));
  Register #(.width(32)) register_9 (.D(WriteDataEX), .en(En), .Q(WriteDataMEM), .clk(clk), .clr(clr));
  Register #(.width(32)) register_10 (.D(JumpAddrEX), .en(En), .Q(JumpAddrMEM), .clk(clk), .clr(clr));
endmodule

module MEM_WB (
  input  clk,
  input  clr,
  input  IsJALMEM,
  input  [31:0] ALUResultMEM,
  input  MemtoRegMEM,
  input  RegWriteMEM,
  input  [31:0] ReadDataMEM,
  input  [31:0] JumpAddrMEM,
  input  [4:0] WriteReg_MEM,
  input  En,
  output IsJALWB,
  output [31:0] ALUResultWB,
  output MemtoRegWB,
  output RegWriteWB,
  output [31:0] ReadDataWB,
  output [31:0] JumpAddrWB,
  output [4:0] WriteReg_WB
);

  Register #(.width(1)) register_1 (.D(IsJALMEM), .en(En), .Q(IsJALWB), .clk(clk), .clr(clr));
  Register #(.width(1)) register_2 (.D(MemtoRegMEM), .en(En), .Q(MemtoRegWB), .clk(clk), .clr(clr));
  Register #(.width(1)) register_3 (.D(RegWriteMEM), .en(En), .Q(RegWriteWB), .clk(clk), .clr(clr));
  Register #(.width(5)) register_4 (.D(WriteReg_MEM), .en(En), .Q(WriteReg_WB), .clk(clk), .clr(clr));
  Register #(.width(32)) register_5 (.D(ALUResultMEM), .en(En), .Q(ALUResultWB), .clk(clk), .clr(clr));
  Register #(.width(32)) register_6 (.D(ReadDataMEM), .en(En), .Q(ReadDataWB), .clk(clk), .clr(clr));
  Register #(.width(32)) register_7 (.D(JumpAddrMEM), .en(En), .Q(JumpAddrWB), .clk(clk), .clr(clr));
endmodule

// Hazard Unit
module HazardUnit (
  input  clk,
  input  ReadRt,
  input  ReadRs,
  input  RegWriteMEM,
  input  [4:0] RS,
  input  [4:0] WriteReg_MEM,
  input  [4:0] WriteReg_EX,
  input  [4:0] RT,
  input  RegWriteEX,
  input  IsLW,
  input  IsToBranchOrJump,
  output [1:0] RsOutput,
  output FlushID,
  output StallIF,
  output StallID,
  output [31:0] BubbleNum,
  output [1:0] RtOutput,
  output FlushIF
);

  wire and_1_out, and_2_out, and_3_out, and_4_out, comparator_1_eq, comparator_2_eq, comparator_3_eq,
       comparator_4_eq, comparator_5_eq, comparator_6_eq, comparator_7_eq, comparator_8_eq, d_ff_1_q,
       d_ff_2_q, not_1_out, not_2_out, not_3_out, not_4_out, or_1_out;
  wire [1:0] multiplexer_1_out, multiplexer_2_out;

  Comparator #(.width(5)) comparator_1 (.a({5{1'b0}}), .b(WriteReg_MEM), .eq(comparator_1_eq));  // open: gt, lt
  Comparator #(.width(5)) comparator_2 (.a(WriteReg_MEM), .b(RS), .eq(comparator_2_eq));  // open: gt, lt
  Comparator #(.width(5)) comparator_3 (.a({5{1'b0}}), .b(WriteReg_EX), .eq(comparator_3_eq));  // open: gt, lt
  Comparator #(.width(5)) comparator_4 (.a(WriteReg_EX), .b(RS), .eq(comparator_4_eq));  // open: gt, lt
  Comparator #(.width(5)) comparator_5 (.a({5{1'b0}}), .b(WriteReg_MEM), .eq(comparator_5_eq));  // open: gt, lt
  Comparator #(.width(5)) comparator_6 (.a(WriteReg_MEM), .b(RT), .eq(comparator_6_eq));  // open: gt, lt
  Comparator #(.width(5)) comparator_7 (.a({5{1'b0}}), .b(WriteReg_EX), .eq(comparator_7_eq));  // open: gt, lt
  Comparator #(.width(5)) comparator_8 (.a(WriteReg_EX), .b(RT), .eq(comparator_8_eq));  // open: gt, lt
  not not_1 (not_1_out, comparator_1_eq);
  not not_2 (not_2_out, comparator_3_eq);
  not not_3 (not_3_out, comparator_5_eq);
  not not_4 (not_4_out, comparator_7_eq);
  and and_1 (and_1_out, ReadRs, RegWriteMEM, not_1_out, comparator_2_eq);
  and and_2 (and_2_out, ReadRs, RegWriteEX, not_2_out, comparator_4_eq);
  and and_3 (and_3_out, ReadRt, RegWriteMEM, not_3_out, comparator_6_eq);
  and and_4 (and_4_out, ReadRt, RegWriteEX, not_4_out, comparator_8_eq);
  Multiplexer #(.width(2), .enable("false")) multiplexer_1 (
    .in0(2'b00), .in1(2'b10), .out(multiplexer_1_out), .sel(and_1_out));
  Multiplexer #(.width(2), .enable("false")) multiplexer_2 (
    .in0(2'b00), .in1(2'b10), .out(multiplexer_2_out), .sel(and_3_out));
  Multiplexer #(.width(2), .enable("false")) multiplexer_3 (
    .in0(multiplexer_1_out), .in1(2'b01), .out(RsOutput), .sel(and_2_out));
  Multiplexer #(.width(2), .enable("false")) multiplexer_4 (
    .in0(multiplexer_2_out), .in1(2'b01), .out(RtOutput), .sel(and_4_out));
  or or_1 (or_1_out, and_2_out, and_4_out);
  and and_5 (StallID, IsLW, or_1_out);
  D_Flip_Flop #(.trigger("falling")) d_ff_1 (
    .clk(clk), .D(IsToBranchOrJump), .Q(d_ff_1_q));  // open: Qn, preset, en, reset
  and and_6 (FlushIF, ~clk, d_ff_1_q);  // AND_Gate
  D_Flip_Flop #(.trigger("falling")) d_ff_2 (.clk(clk), .D(StallID), .Q(d_ff_2_q));  // open: Qn, preset, en, reset
  Counter #(.width(32), .max('hffffffff)) counter_1 (
    .count(StallID), .Q(BubbleNum), .clk(clk));  // open: load, D, carry, clr
  and and_7 (FlushID, clk, d_ff_2_q);

  assign StallIF = StallID;

  // Other names for the same wires on the sheet: ReadWriteEX = RegWriteEX; ReadWriteMEM = RegWriteMEM

  // Notes on the sheet:
  //   Rt Hazard in EX
  //   Rs Hazard in MEM
  //   Rs Hazard in EX
  //   hasHazard
endmodule

// FunDecoder
module FDecoder (
  input  F5,
  input  F4,
  input  F3,
  input  F2,
  input  F1,
  input  F0,
  output Out2,
  output Out1,
  output Out0,
  output JR
);

  wire and_2_out, and_3_out, and_4_out, and_5_out, and_6_out, not_1_out, not_2_out, not_3_out, not_4_out,
       not_5_out, not_6_out, not_7_out, not_8_out, not_9_out, not_10_out, not_11_out, not_12_out, not_13_out;

  not not_1 (not_1_out, F5);
  not not_2 (not_2_out, F4);
  not not_3 (not_3_out, F2);
  not not_4 (not_4_out, F1);
  not not_5 (not_5_out, F2);
  not not_6 (not_6_out, F1);
  not not_7 (not_7_out, F1);
  not not_8 (not_8_out, F2);
  not not_9 (not_9_out, F5);
  not not_10 (not_10_out, F1);
  not not_11 (not_11_out, F0);
  and and_1 (JR, not_1_out, not_2_out, F3, not_3_out, not_4_out, F0);
  not not_12 (not_12_out, F5);
  and and_2 (and_2_out, not_5_out, not_6_out);
  or or_1 (Out2, not_12_out, and_2_out, and_3_out);
  and and_3 (and_3_out, not_7_out, F0);
  not not_13 (not_13_out, F5);
  or or_2 (Out1, not_13_out, and_4_out);
  and and_4 (and_4_out, not_8_out, F1);
  and and_5 (and_5_out, not_9_out, F1);
  or or_3 (Out0, and_5_out, F3, and_6_out);
  and and_6 (and_6_out, F5, not_10_out, not_11_out);
endmodule
